// Logisim project ACM1401_U201414620_胡汉鹏_regfile.circ as structural Verilog: 4 circuits, main circuit main
module main (
  input  [4:0] Reg1_num,
  input  [4:0] Reg2,
  input  [4:0] Write_Reg_num,
  input  [31:0] Din,
  input  Write_Enable,
  input  Clock,
  output [31:0] Reg1,
  output [31:0] v0_Value,
  output [31:0] a0_Value,
  output [31:0] s2_Value,
  output [31:0] ra_Value,
  output [31:0] Reg2_2
);

  wire demultiplexer_5_out0, demultiplexer_5_out1, demultiplexer_5_out2, demultiplexer_5_out3,
       demultiplexer_11_out0, demultiplexer_11_out1, demultiplexer_15_out0, demultiplexer_15_out1,
       demultiplexer_15_out2, demultiplexer_15_out3, E0, E1, E2, E3, E4, E5, E6, E7, E8, E9, E10, E11, E12,
       E13, E14, E15, E16, E17, E18, E19, E20, E21, E22, E23, E24, E25, E26, E27, E28, E29, E30, E31;
  wire [31:0] demultiplexer_7_out0, demultiplexer_7_out1, demultiplexer_7_out2, demultiplexer_7_out3,
       demultiplexer_12_out0, demultiplexer_12_out1, demultiplexer_17_out0, demultiplexer_17_out1,
       demultiplexer_17_out2, demultiplexer_17_out3, multiplexer_1_out, multiplexer_2_out, multiplexer_3_out,
       multiplexer_4_out, multiplexer_5_out, multiplexer_6_out, multiplexer_7_out, multiplexer_8_out,
       multiplexer_9_out, multiplexer_10_out, multiplexer_13_out, multiplexer_14_out, multiplexer_15_out,
       multiplexer_16_out, multiplexer_17_out, multiplexer_18_out, multiplexer_19_out, multiplexer_20_out,
       multiplexer_21_out, multiplexer_22_out, R0, R1, R3, R5, R6, R7, R8, R9, R10, R11, R12, R13, R14, R15,
       R16, R17, R18, R19, R20, R21, R22, R23, R24, R25, R26, R27, R28, R30, W0, W1, W2, W3, W4, W5, W6, W7,
       W8, W9, W10, W11, W12, W13, W14, W15, W16, W17, W18, W19, W20, W21, W22, W23, W24, W25, W26, W27, W28,
       W29, W30, W31;

  Multiplexer #(.select(2), .width(32), .enable("false")) multiplexer_1 (
    .in0(R0), .in1(R1), .in2(v0_Value), .in3(R3), .out(multiplexer_1_out), .sel(Reg1_num[1:0]));
  Multiplexer #(.select(2), .width(32), .enable("false")) multiplexer_2 (
    .in0(R0), .in1(R1), .in2(v0_Value), .in3(R3), .out(multiplexer_2_out), .sel(Reg2[1:0]));
  Demultiplexer #(.select(2), .disabled(0), .enable("false")) demultiplexer_1 (
    .out0(E0), .out1(E1), .out2(E2), .out3(E3), .in(demultiplexer_5_out0), .sel(Write_Reg_num[1:0]));
  Demultiplexer #(.select(2), .width(32), .disabled(0), .enable("false")) demultiplexer_2 (
    .out0(W0), .out1(W1), .out2(W2), .out3(W3), .in(demultiplexer_7_out0), .sel(Write_Reg_num[1:0]));
  Multiplexer #(.select(2), .width(32), .enable("false")) multiplexer_3 (
    .in0(a0_Value), .in1(R5), .in2(R6), .in3(R7), .out(multiplexer_3_out), .sel(Reg1_num[1:0]));
  Multiplexer #(.select(2), .width(32), .enable("false")) multiplexer_4 (
    .in0(a0_Value), .in1(R5), .in2(R6), .in3(R7), .out(multiplexer_4_out), .sel(Reg2[1:0]));
  Demultiplexer #(.select(2), .disabled(0), .enable("false")) demultiplexer_3 (
    .out0(E4), .out1(E5), .out2(E6), .out3(E7), .in(demultiplexer_5_out1), .sel(Write_Reg_num[1:0]));
  Demultiplexer #(.select(2), .width(32), .disabled(0), .enable("false")) demultiplexer_4 (
    .out0(W4), .out1(W5), .out2(W6), .out3(W7), .in(demultiplexer_7_out1), .sel(Write_Reg_num[1:0]));
  Register #(.width(32)) register_1 (.D({32{1'b0}}), .en(1'b0), .Q(R0), .clk(Clock), .clr(1'b0));
  Register #(.width(32)) register_2 (.D(W8), .en(E8), .Q(R8), .clk(Clock), .clr(1'b0));
  Register #(.width(32)) register_3 (.D(W16), .en(E16), .Q(R16), .clk(Clock), .clr(1'b0));
  Register #(.width(32)) register_4 (.D(W24), .en(E24), .Q(R24), .clk(Clock), .clr(1'b0));
  Multiplexer #(.select(2), .width(32), .enable("false")) multiplexer_5 (
    .in0(multiplexer_1_out), .in1(multiplexer_3_out), .in2(multiplexer_6_out), .in3(multiplexer_9_out),
    .out(multiplexer_5_out), .sel(Reg1_num[3:2]));
  Multiplexer #(.select(2), .width(32), .enable("false")) multiplexer_6 (
    .in0(R8), .in1(R9), .in2(R10), .in3(R11), .out(multiplexer_6_out), .sel(Reg1_num[1:0]));
  Multiplexer #(.select(2), .width(32), .enable("false")) multiplexer_7 (
    .in0(multiplexer_2_out), .in1(multiplexer_4_out), .in2(multiplexer_8_out), .in3(multiplexer_10_out),
    .out(multiplexer_7_out), .sel(Reg2[3:2]));
  Multiplexer #(.select(2), .width(32), .enable("false")) multiplexer_8 (
    .in0(R8), .in1(R9), .in2(R10), .in3(R11), .out(multiplexer_8_out), .sel(Reg2[1:0]));
  Demultiplexer #(.select(2), .disabled(0), .enable("false")) demultiplexer_5 (
    .out0(demultiplexer_5_out0), .out1(demultiplexer_5_out1), .out2(demultiplexer_5_out2),
    .out3(demultiplexer_5_out3), .in(demultiplexer_11_out0), .sel(Write_Reg_num[3:2]));
  Demultiplexer #(.select(2), .disabled(0), .enable("false")) demultiplexer_6 (
    .out0(E8), .out1(E9), .out2(E10), .out3(E11), .in(demultiplexer_5_out2), .sel(Write_Reg_num[1:0]));
  Demultiplexer #(.select(2), .width(32), .disabled(0), .enable("false")) demultiplexer_7 (
    .out0(demultiplexer_7_out0), .out1(demultiplexer_7_out1), .out2(demultiplexer_7_out2),
    .out3(demultiplexer_7_out3), .in(demultiplexer_12_out0), .sel(Write_Reg_num[3:2]));
  Demultiplexer #(.select(2), .width(32), .disabled(0), .enable("false")) demultiplexer_8 (
    .out0(W8), .out1(W9), .out2(W10), .out3(W11), .in(demultiplexer_7_out2), .sel(Write_Reg_num[1:0]));
  Register #(.width(32)) register_5 (.D(W1), .en(E1), .Q(R1), .clk(Clock), .clr(1'b0));
  Register #(.width(32)) register_6 (.D(W9), .en(E9), .Q(R9), .clk(Clock), .clr(1'b0));
  Register #(.width(32)) register_7 (.D(W17), .en(E17), .Q(R17), .clk(Clock), .clr(1'b0));
  Register #(.width(32)) register_8 (.D(W25), .en(E25), .Q(R25), .clk(Clock), .clr(1'b0));
  Multiplexer #(.select(2), .width(32), .enable("false")) multiplexer_9 (
    .in0(R12), .in1(R13), .in2(R14), .in3(R15), .out(multiplexer_9_out), .sel(Reg1_num[1:0]));
  Multiplexer #(.select(2), .width(32), .enable("false")) multiplexer_10 (
    .in0(R12), .in1(R13), .in2(R14), .in3(R15), .out(multiplexer_10_out), .sel(Reg2[1:0]));
  Demultiplexer #(.select(2), .disabled(0), .enable("false")) demultiplexer_9 (
    .out0(E12), .out1(E13), .out2(E14), .out3(E15), .in(demultiplexer_5_out3), .sel(Write_Reg_num[1:0]));
  Demultiplexer #(.select(2), .width(32), .disabled(0), .enable("false")) demultiplexer_10 (
    .out0(W12), .out1(W13), .out2(W14), .out3(W15), .in(demultiplexer_7_out3), .sel(Write_Reg_num[1:0]));
  Register #(.width(32)) register_9 (.D(W2), .en(E2), .Q(v0_Value), .clk(Clock), .clr(1'b0));
  Register #(.width(32)) register_10 (.D(W10), .en(E10), .Q(R10), .clk(Clock), .clr(1'b0));
  Register #(.width(32)) register_11 (.D(W18), .en(E18), .Q(R18), .clk(Clock), .clr(1'b0));
  Register #(.width(32)) register_12 (.D(W26), .en(E26), .Q(R26), .clk(Clock), .clr(1'b0));
  Multiplexer #(.width(32), .enable("false")) multiplexer_11 (
    .in0(multiplexer_5_out), .in1(multiplexer_15_out), .out(Reg1), .sel(Reg1_num[4]));
  Multiplexer #(.width(32), .enable("false")) multiplexer_12 (
    .in0(multiplexer_7_out), .in1(multiplexer_17_out), .out(Reg2_2), .sel(Reg2[4]));
  Demultiplexer #(.disabled(0), .enable("false")) demultiplexer_11 (
    .out0(demultiplexer_11_out0), .out1(demultiplexer_11_out1), .in(Write_Enable), .sel(Write_Reg_num[4]));
  Demultiplexer #(.width(32), .disabled(0), .enable("false")) demultiplexer_12 (
    .out0(demultiplexer_12_out0), .out1(demultiplexer_12_out1), .in(Din), .sel(Write_Reg_num[4]));
  Register #(.width(32)) register_13 (.D(W3), .en(E3), .Q(R3), .clk(Clock), .clr(1'b0));
  Register #(.width(32)) register_14 (.D(W11), .en(E11), .Q(R11), .clk(Clock), .clr(1'b0));
  Register #(.width(32)) register_15 (.D(W19), .en(E19), .Q(R19), .clk(Clock), .clr(1'b0));
  Register #(.width(32)) register_16 (.D(W27), .en(E27), .Q(R27), .clk(Clock), .clr(1'b0));
  Multiplexer #(.select(2), .width(32), .enable("false")) multiplexer_13 (
    .in0(R16), .in1(R17), .in2(R18), .in3(R19), .out(multiplexer_13_out), .sel(Reg1_num[1:0]));
  Multiplexer #(.select(2), .width(32), .enable("false")) multiplexer_14 (
    .in0(R16), .in1(R17), .in2(R18), .in3(R19), .out(multiplexer_14_out), .sel(Reg2[1:0]));
  Demultiplexer #(.select(2), .disabled(0), .enable("false")) demultiplexer_13 (
    .out0(E16), .out1(E17), .out2(E18), .out3(E19), .in(demultiplexer_15_out0), .sel(Write_Reg_num[1:0]));
  Demultiplexer #(.select(2), .width(32), .disabled(0), .enable("false")) demultiplexer_14 (
    .out0(W16), .out1(W17), .out2(W18), .out3(W19), .in(demultiplexer_17_out0), .sel(Write_Reg_num[1:0]));
  Register #(.width(32)) register_17 (.D(W4), .en(E4), .Q(a0_Value), .clk(Clock), .clr(1'b0));
  Register #(.width(32)) register_18 (.D(W12), .en(E12), .Q(R12), .clk(Clock), .clr(1'b0));
  Register #(.width(32)) register_19 (.D(W20), .en(E20), .Q(R20), .clk(Clock), .clr(1'b0));
  Register #(.width(32)) register_20 (.D(W28), .en(E28), .Q(R28), .clk(Clock), .clr(1'b0));
  Multiplexer #(.select(2), .width(32), .enable("false")) multiplexer_15 (
    .in0(multiplexer_13_out), .in1(multiplexer_16_out), .in2(multiplexer_19_out), .in3(multiplexer_21_out),
    .out(multiplexer_15_out), .sel(Reg1_num[3:2]));
  Multiplexer #(.select(2), .width(32), .enable("false")) multiplexer_16 (
    .in0(R20), .in1(R21), .in2(R22), .in3(R23), .out(multiplexer_16_out), .sel(Reg1_num[1:0]));
  Multiplexer #(.select(2), .width(32), .enable("false")) multiplexer_17 (
    .in0(multiplexer_14_out), .in1(multiplexer_18_out), .in2(multiplexer_20_out), .in3(multiplexer_22_out),
    .out(multiplexer_17_out), .sel(Reg2[3:2]));
  Multiplexer #(.select(2), .width(32), .enable("false")) multiplexer_18 (
    .in0(R20), .in1(R21), .in2(R22), .in3(R23), .out(multiplexer_18_out), .sel(Reg2[1:0]));
  Demultiplexer #(.select(2), .disabled(0), .enable("false")) demultiplexer_15 (
    .out0(demultiplexer_15_out0), .out1(demultiplexer_15_out1), .out2(demultiplexer_15_out2),
    .out3(demultiplexer_15_out3), .in(demultiplexer_11_out1), .sel(Write_Reg_num[3:2]));
  Demultiplexer #(.select(2), .disabled(0), .enable("false")) demultiplexer_16 (
    .out0(E20), .out1(E21), .out2(E22), .out3(E23), .in(demultiplexer_15_out1), .sel(Write_Reg_num[1:0]));
  Demultiplexer #(.select(2), .width(32), .disabled(0), .enable("false")) demultiplexer_17 (
    .out0(demultiplexer_17_out0), .out1(demultiplexer_17_out1), .out2(demultiplexer_17_out2),
    .out3(demultiplexer_17_out3), .in(demultiplexer_12_out1), .sel(Write_Reg_num[3:2]));
  Demultiplexer #(.select(2), .width(32), .disabled(0), .enable("false")) demultiplexer_18 (
    .out0(W20), .out1(W21), .out2(W22), .out3(W23), .in(demultiplexer_17_out1), .sel(Write_Reg_num[1:0]));
  Register #(.width(32)) register_21 (.D(W5), .en(E5), .Q(R5), .clk(Clock), .clr(1'b0));
  Register #(.width(32)) register_22 (.D(W13), .en(E13), .Q(R13), .clk(Clock), .clr(1'b0));
  Register #(.width(32)) register_23 (.D(W21), .en(E21), .Q(R21), .clk(Clock), .clr(1'b0));
  Register #(.width(32)) register_24 (.D(W29), .en(E29), .Q(s2_Value), .clk(Clock), .clr(1'b0));
  Multiplexer #(.select(2), .width(32), .enable("false")) multiplexer_19 (
    .in0(R24), .in1(R25), .in2(R26), .in3(R27), .out(multiplexer_19_out), .sel(Reg1_num[1:0]));
  Multiplexer #(.select(2), .width(32), .enable("false")) multiplexer_20 (
    .in0(R24), .in1(R25), .in2(R26), .in3(R27), .out(multiplexer_20_out), .sel(Reg2[1:0]));
  Demultiplexer #(.select(2), .disabled(0), .enable("false")) demultiplexer_19 (
    .out0(E24), .out1(E25), .out2(E26), .out3(E27), .in(demultiplexer_15_out2), .sel(Write_Reg_num[1:0]));
  Demultiplexer #(.select(2), .width(32), .disabled(0), .enable("false")) demultiplexer_20 (
    .out0(W24), .out1(W25), .out2(W26), .out3(W27), .in(demultiplexer_17_out2), .sel(Write_Reg_num[1:0]));
  Register #(.width(32)) register_25 (.D(W6), .en(E6), .Q(R6), .clk(Clock), .clr(1'b0));
  Register #(.width(32)) register_26 (.D(W14), .en(E14), .Q(R14), .clk(Clock), .clr(1'b0));
  Register #(.width(32)) register_27 (.D(W22), .en(E22), .Q(R22), .clk(Clock), .clr(1'b0));
  Register #(.width(32)) register_28 (.D(W30), .en(E30), .Q(R30), .clk(Clock), .clr(1'b0));
  Multiplexer #(.select(2), .width(32), .enable("false")) multiplexer_21 (
    .in0(R28), .in1(s2_Value), .in2(R30), .in3(ra_Value), .out(multiplexer_21_out), .sel(Reg1_num[1:0]));
  Multiplexer #(.select(2), .width(32), .enable("false")) multiplexer_22 (
    .in0(R28), .in1(s2_Value), .in2(R30), .in3(ra_Value), .out(multiplexer_22_out), .sel(Reg2[1:0]));
  Demultiplexer #(.select(2), .disabled(0), .enable("false")) demultiplexer_21 (
    .out0(E28), .out1(E29), .out2(E30), .out3(E31), .in(demultiplexer_15_out3), .sel(Write_Reg_num[1:0]));
  Demultiplexer #(.select(2), .width(32), .disabled(0), .enable("false")) demultiplexer_22 (
    .out0(W28), .out1(W29), .out2(W30), .out3(W31), .in(demultiplexer_17_out3), .sel(Write_Reg_num[1:0]));
  Register #(.width(32)) register_29 (.D(W7), .en(E7), .Q(R7), .clk(Clock), .clr(1'b0));
  Register #(.width(32)) register_30 (.D(W15), .en(E15), .Q(R15), .clk(Clock), .clr(1'b0));
  Register #(.width(32)) register_31 (.D(W23), .en(E23), .Q(R23), .clk(Clock), .clr(1'b0));
  Register #(.width(32)) register_32 (.D(W31), .en(E31), .Q(ra_Value), .clk(Clock), .clr(1'b0));

  // Other names for the same wires on the sheet: clk = Clock; R2[31:0] = v0_Value; s0[31:0] = v0_Value;
  //   R4[31:0] = a0_Value; s1[31:0] = a0_Value; R29[31:0] = s2_Value; s2[31:0] = s2_Value; R31[31:0] = ra_Value;
  //   ra[31:0] = ra_Value; reg2_num[4:0] = Reg2; reg2_t[31:0] = Reg2_2; WE = Write_Enable; write_data[31:0] = Din

  // Notes on the sheet:
  //   输入引脚
  //   输出引脚
  //   Debug引脚，便于观测寄存器值
  //   请勿修改引脚以及封装，直接使用隧道连接电路
endmodule

module test (
  input  [31:0] in_1,
  input  [31:0] in_2,
  input  [31:0] in_3,
  input  [31:0] in_4,
  input  [31:0] in_5,
  input  in_6,
  output OF,
  output CF,
  output Equal
);

  wire buffer_1_out, buffer_2_out, button_1_out, Clock, counter_1_carry, not_1_out, not_3_out, undriven, we;
  wire [4:0] adress;
  wire [5:0] counter_1_q;
  wire [15:0] main_1_reg1, SUM, Y;
  wire [31:0] multiplexer_2_out, multiplexer_4_out, ram_1_data, X;
  wire [31:16] alu_1_result;

  Hex_Digit_Display hex_digit_display_1 (.value(4'b0000));  // open: dp
  Clock clock_1 (.out(Clock));
  Button button_1 (.out(button_1_out));
  // Probe on adress
  Hex_Digit_Display hex_digit_display_2 (.value(4'b0000));  // open: dp
  Counter #(.width(6), .max('h20), .ongoal("stay")) counter_1 (
    .count(1'b1), .Q(counter_1_q), .carry(counter_1_carry), .clk(not_1_out), .clr(button_1_out));  // open: load, D
  not not_1 (not_1_out, Clock);
  Hex_Digit_Display hex_digit_display_3 (.value(4'b0000));  // open: dp
  Hex_Digit_Display hex_digit_display_4 (.value(4'b0000));  // open: dp
  not not_2 (we, counter_1_carry);
  // Probe on counter_1_carry
  buf buffer_1 (buffer_1_out, Clock);
  Hex_Digit_Display hex_digit_display_5 (.value(SUM[15:12]));  // open: dp
  Hex_Digit_Display hex_digit_display_6 (.value(SUM[11:8]));  // open: dp
  Multiplexer #(.width(5)) multiplexer_1 (.in0({5{1'b1}}), .in1(counter_1_q[4:0]), .out(adress), .sel(we));  // open: en
  buf buffer_2 (buffer_2_out, buffer_1_out);
  // Probe on X
  Hex_Digit_Display hex_digit_display_7 (.value(SUM[7:4]));  // open: dp
  Multiplexer #(.width(32)) multiplexer_2 (
    .in0({Y, main_1_reg1}), .in1(in_5), .out(multiplexer_2_out), .sel(in_6));  // open: en
  Hex_Digit_Display hex_digit_display_8 (.value(SUM[3:0]));  // open: dp
  RAM #(.addrWidth(5), .dataWidth(32), .bus("separate")) ram_1 (
    .addr(adress), .din(multiplexer_2_out), .data(ram_1_data), .str(buffer_2_out), .sel(undriven),
    .clk(not_1_out), .ld(not_1_out));  // open: clr
  not not_3 (not_3_out, not_1_out);
  // Probe on {{16{1'b0}}, Y}
  Multiplexer #(.width(32)) multiplexer_3 (.in0(ram_1_data), .in1({32{1'b0}}), .out(X), .sel(not_3_out));  // open: en
  ALU alu_1 (
    .AluOP(4'b0101), .X(X), .Equal(Equal), .Result({alu_1_result, SUM}), .Signed_Overflow(OF),
    .Y({{16{1'b0}}, Y}), .UnSigned_Overflow(CF));  // open: Result_2
  // Probe on {{16{1'b0}}, SUM}
  // Probe on SUM
  Multiplexer #(.width(32)) multiplexer_4 (
    .in0({SUM, ram_1_data[15:0]}), .in1({32{1'b0}}), .out(multiplexer_4_out), .sel(in_6));  // open: en
  main main_1 (
    .Reg1_num(5'b00010), .Write_Reg_num(5'b00010), .Din(multiplexer_4_out), .Write_Enable(we),
    .Clock(buffer_2_out), .Reg1({Y, main_1_reg1}), .v0_Value(in_1), .a0_Value(in_2), .s2_Value(in_3),
    .ra_Value(in_4));  // open: Reg2, Reg2_2

  // Other names for the same wires on the sheet: on = in_6; s0[31:0] = in_1; s1[31:0] = in_2; s2[31:0] = in_3;
  //   s3[31:0] = in_4
endmodule

module test2 (
  input  [31:0] in_1,
  input  in_2,
  output OF,
  output CF,
  output Equal
);

  wire buffer_1_out, buffer_2_out, button_1_out, Clock, counter_1_carry, not_1_out, not_3_out, or_1_out,
       undriven, we;
  wire [5:0] adress, counter_1_q;
  wire [31:0] multiplexer_2_out, ram_1_data, SUM, X, Y;

  Hex_Digit_Display hex_digit_display_1 (.value(SUM[31:28]));  // open: dp
  Button button_1 (.out(button_1_out));
  // Probe on adress
  Hex_Digit_Display hex_digit_display_2 (.value(SUM[27:24]));  // open: dp
  Counter #(.width(6), .max('h20), .ongoal("stay")) counter_1 (
    .count(1'b1), .Q(counter_1_q), .carry(counter_1_carry), .clk(not_1_out), .clr(button_1_out));  // open: load, D
  not not_1 (not_1_out, Clock);
  Hex_Digit_Display hex_digit_display_3 (.value(SUM[19:16]));  // open: dp
  Hex_Digit_Display hex_digit_display_4 (.value(SUM[23:20]));  // open: dp
  not not_2 (we, counter_1_carry);
  // Probe on counter_1_carry
  buf buffer_1 (buffer_1_out, Clock);
  buf buffer_2 (buffer_2_out, buffer_1_out);
  Hex_Digit_Display hex_digit_display_5 (.value(SUM[15:12]));  // open: dp
  Hex_Digit_Display hex_digit_display_6 (.value(SUM[11:8]));  // open: dp
  // Probe on adress
  Multiplexer #(.width(5)) multiplexer_1 (
    .in0({5{1'b1}}), .in1(counter_1_q[4:0]), .out(adress[4:0]), .sel(we));  // open: en
  and and_1 (adress[5], buffer_2_out, ~in_2);  // AND_Gate
  // Probe on X
  Hex_Digit_Display hex_digit_display_7 (.value(SUM[7:4]));  // open: dp
  Multiplexer #(.width(32)) multiplexer_2 (.in0(Y), .in1(in_1), .out(multiplexer_2_out), .sel(in_2));  // open: en
  Hex_Digit_Display hex_digit_display_8 (.value(SUM[3:0]));  // open: dp
  Clock clock_1 (.out(Clock));
  RAM #(.addrWidth(6), .dataWidth(32), .bus("separate")) ram_1 (
    .addr(adress), .din(multiplexer_2_out), .data(ram_1_data), .str(buffer_2_out), .sel(undriven),
    .clk(not_1_out), .ld(not_1_out));  // open: clr
  not not_3 (not_3_out, not_1_out);
  // Probe on Y
  // Probe on Y
  // Probe on X
  Multiplexer #(.width(32)) multiplexer_3 (.in0(ram_1_data), .in1({32{1'b0}}), .out(X), .sel(or_1_out));  // open: en
  or or_1 (or_1_out, not_3_out, ~we);  // OR_Gate
  ALU alu_1 (
    .AluOP(4'b0101), .X(X), .Equal(Equal), .Result(SUM), .Signed_Overflow(OF), .Y(Y), .UnSigned_Overflow(CF));  // open: Result_2
  // Probe on SUM
  // Probe on SUM
  main main_1 (
    .Reg1_num(5'b00010), .Write_Reg_num(5'b00010), .Din(SUM), .Write_Enable(we), .Clock(buffer_2_out),
    .Reg1(Y));  // open: Reg2, Reg2_2, v0_Value, a0_Value, s2_Value, ra_Value

  // Other names for the same wires on the sheet: s = adress[5]
endmodule

module main2 (
  input  [4:0] Reg1_num,
  input  [4:0] Reg2,
  input  [4:0] Write_Reg_num,
  input  [31:0] Din,
  input  Write_Enable,
  input  Clock,
  output [31:0] Reg1,
  output [31:0] s0_Value,
  output [31:0] s1_Value,
  output [31:0] s2_Value,
  output [31:0] ra_Value,
  output [31:0] Reg2_2
);

  wire [31:0] demultiplexer_3_out0, demultiplexer_3_out1, demultiplexer_3_out2, demultiplexer_3_out3,
       demultiplexer_6_out0, demultiplexer_6_out1, demultiplexer_8_out0, demultiplexer_8_out1,
       demultiplexer_8_out2, demultiplexer_8_out3, multiplexer_1_out, multiplexer_2_out, multiplexer_3_out,
       multiplexer_4_out, multiplexer_5_out, multiplexer_6_out, multiplexer_7_out, multiplexer_8_out,
       multiplexer_9_out, multiplexer_10_out, multiplexer_13_out, multiplexer_14_out, multiplexer_15_out,
       multiplexer_16_out, multiplexer_17_out, multiplexer_18_out, multiplexer_19_out, multiplexer_20_out,
       multiplexer_21_out, multiplexer_22_out, R0, R1, R2, R3, R4, R5, R6, R7, R8, R9, R10, R11, R12, R13,
       R14, R15, R19, R20, R21, R22, R23, R24, R25, R26, R27, R28, R29, R30, W0, W1, W2, W3, W4, W5, W6, W7,
       W8, W9, W10, W11, W12, W13, W14, W15, W16, W17, W18, W19, W20, W21, W22, W23, W24, W25, W26, W27, W28,
       W29, W30, W31;

  Multiplexer #(.select(2), .width(32)) multiplexer_1 (
    .in0(R0), .in1(R1), .in2(R2), .in3(R3), .out(multiplexer_1_out), .sel(Reg1_num[1:0]));  // open: en
  Multiplexer #(.select(2), .width(32)) multiplexer_2 (
    .in0(R0), .in1(R1), .in2(R2), .in3(R3), .out(multiplexer_2_out), .sel(Reg2[1:0]));  // open: en
  Demultiplexer #(.select(2), .width(32)) demultiplexer_1 (
    .out0(W0), .out1(W1), .out2(W2), .out3(W3), .in(demultiplexer_3_out0), .sel(Write_Reg_num[1:0]));  // open: en
  Multiplexer #(.select(2), .width(32)) multiplexer_3 (
    .in0(R4), .in1(R5), .in2(R6), .in3(R7), .out(multiplexer_3_out), .sel(Reg1_num[1:0]));  // open: en
  Multiplexer #(.select(2), .width(32)) multiplexer_4 (
    .in0(R4), .in1(R5), .in2(R6), .in3(R7), .out(multiplexer_4_out), .sel(Reg2[1:0]));  // open: en
  Demultiplexer #(.select(2), .width(32)) demultiplexer_2 (
    .out0(W4), .out1(W5), .out2(W6), .out3(W7), .in(demultiplexer_3_out1), .sel(Write_Reg_num[1:0]));  // open: en
  Register #(.width(32)) register_1 (.D(W0), .en(1'b0), .Q(R0), .clk(Clock));  // open: clr
  Register #(.width(32)) register_2 (.D(W8), .en(Write_Enable), .Q(R8), .clk(Clock));  // open: clr
  Register #(.width(32)) register_3 (.D(W16), .en(Write_Enable), .Q(s0_Value), .clk(Clock));  // open: clr
  Register #(.width(32)) register_4 (.D(W24), .en(Write_Enable), .Q(R24), .clk(Clock));  // open: clr
  Multiplexer #(.select(2), .width(32)) multiplexer_5 (
    .in0(multiplexer_1_out), .in1(multiplexer_3_out), .in2(multiplexer_6_out), .in3(multiplexer_9_out),
    .out(multiplexer_5_out), .sel(Reg1_num[3:2]));  // open: en
  Multiplexer #(.select(2), .width(32)) multiplexer_6 (
    .in0(R8), .in1(R9), .in2(R10), .in3(R11), .out(multiplexer_6_out), .sel(Reg1_num[1:0]));  // open: en
  Multiplexer #(.select(2), .width(32)) multiplexer_7 (
    .in0(multiplexer_2_out), .in1(multiplexer_4_out), .in2(multiplexer_8_out), .in3(multiplexer_10_out),
    .out(multiplexer_7_out), .sel(Reg2[3:2]));  // open: en
  Multiplexer #(.select(2), .width(32)) multiplexer_8 (
    .in0(R8), .in1(R9), .in2(R10), .in3(R11), .out(multiplexer_8_out), .sel(Reg2[1:0]));  // open: en
  Demultiplexer #(.select(2), .width(32)) demultiplexer_3 (
    .out0(demultiplexer_3_out0), .out1(demultiplexer_3_out1), .out2(demultiplexer_3_out2),
    .out3(demultiplexer_3_out3), .in(demultiplexer_6_out0), .sel(Write_Reg_num[3:2]));  // open: en
  Demultiplexer #(.select(2), .width(32)) demultiplexer_4 (
    .out0(W8), .out1(W9), .out2(W10), .out3(W11), .in(demultiplexer_3_out2), .sel(Write_Reg_num[1:0]));  // open: en
  Register #(.width(32)) register_5 (.D(W1), .en(Write_Enable), .Q(R1), .clk(Clock));  // open: clr
  Register #(.width(32)) register_6 (.D(W9), .en(Write_Enable), .Q(R9), .clk(Clock));  // open: clr
  Register #(.width(32)) register_7 (.D(W17), .en(Write_Enable), .Q(s1_Value), .clk(Clock));  // open: clr
  Register #(.width(32)) register_8 (.D(W25), .en(Write_Enable), .Q(R25), .clk(Clock));  // open: clr
  Multiplexer #(.select(2), .width(32)) multiplexer_9 (
    .in0(R12), .in1(R13), .in2(R14), .in3(R15), .out(multiplexer_9_out), .sel(Reg1_num[1:0]));  // open: en
  Multiplexer #(.select(2), .width(32)) multiplexer_10 (
    .in0(R12), .in1(R13), .in2(R14), .in3(R15), .out(multiplexer_10_out), .sel(Reg2[1:0]));  // open: en
  Demultiplexer #(.select(2), .width(32)) demultiplexer_5 (
    .out0(W12), .out1(W13), .out2(W14), .out3(W15), .in(demultiplexer_3_out3), .sel(Write_Reg_num[1:0]));  // open: en
  Register #(.width(32)) register_9 (.D(W2), .en(Write_Enable), .Q(R2), .clk(Clock));  // open: clr
  Register #(.width(32)) register_10 (.D(W10), .en(Write_Enable), .Q(R10), .clk(Clock));  // open: clr
  Register #(.width(32)) register_11 (.D(W18), .en(Write_Enable), .Q(s2_Value), .clk(Clock));  // open: clr
  Register #(.width(32)) register_12 (.D(W26), .en(Write_Enable), .Q(R26), .clk(Clock));  // open: clr
  Multiplexer #(.width(32)) multiplexer_11 (
    .in0(multiplexer_5_out), .in1(multiplexer_15_out), .out(Reg1), .sel(Reg1_num[4]));  // open: en
  Multiplexer #(.width(32)) multiplexer_12 (
    .in0(multiplexer_7_out), .in1(multiplexer_17_out), .out(Reg2_2), .sel(Reg2[4]));  // open: en
  Demultiplexer #(.width(32)) demultiplexer_6 (
    .out0(demultiplexer_6_out0), .out1(demultiplexer_6_out1), .in(Din), .sel(Write_Reg_num[4]));  // open: en
  Register #(.width(32)) register_13 (.D(W3), .en(Write_Enable), .Q(R3), .clk(Clock));  // open: clr
  Register #(.width(32)) register_14 (.D(W11), .en(Write_Enable), .Q(R11), .clk(Clock));  // open: clr
  Register #(.width(32)) register_15 (.D(W19), .en(Write_Enable), .Q(R19), .clk(Clock));  // open: clr
  Register #(.width(32)) register_16 (.D(W27), .en(Write_Enable), .Q(R27), .clk(Clock));  // open: clr
  Multiplexer #(.select(2), .width(32)) multiplexer_13 (
    .in0(s0_Value), .in1(s1_Value), .in2(s2_Value), .in3(R19), .out(multiplexer_13_out), .sel(Reg1_num[1:0]));  // open: en
  Multiplexer #(.select(2), .width(32)) multiplexer_14 (
    .in0(s0_Value), .in1(s1_Value), .in2(s2_Value), .in3(R19), .out(multiplexer_14_out), .sel(Reg2[1:0]));  // open: en
  Demultiplexer #(.select(2), .width(32)) demultiplexer_7 (
    .out0(W16), .out1(W17), .out2(W18), .out3(W19), .in(demultiplexer_8_out0), .sel(Write_Reg_num[1:0]));  // open: en
  Register #(.width(32)) register_17 (.D(W4), .en(Write_Enable), .Q(R4), .clk(Clock));  // open: clr
  Register #(.width(32)) register_18 (.D(W12), .en(Write_Enable), .Q(R12), .clk(Clock));  // open: clr
  Register #(.width(32)) register_19 (.D(W20), .en(Write_Enable), .Q(R20), .clk(Clock));  // open: clr
  Register #(.width(32)) register_20 (.D(W28), .en(Write_Enable), .Q(R28), .clk(Clock));  // open: clr
  Multiplexer #(.select(2), .width(32)) multiplexer_15 (
    .in0(multiplexer_13_out), .in1(multiplexer_16_out), .in2(multiplexer_19_out), .in3(multiplexer_21_out),
    .out(multiplexer_15_out), .sel(Reg1_num[3:2]));  // open: en
  Multiplexer #(.select(2), .width(32)) multiplexer_16 (
    .in0(R20), .in1(R21), .in2(R22), .in3(R23), .out(multiplexer_16_out), .sel(Reg1_num[1:0]));  // open: en
  Multiplexer #(.select(2), .width(32)) multiplexer_17 (
    .in0(multiplexer_14_out), .in1(multiplexer_18_out), .in2(multiplexer_20_out), .in3(multiplexer_22_out),
    .out(multiplexer_17_out), .sel(Reg2[3:2]));  // open: en
  Multiplexer #(.select(2), .width(32)) multiplexer_18 (
    .in0(R20), .in1(R21), .in2(R22), .in3(R23), .out(multiplexer_18_out), .sel(Reg2[1:0]));  // open: en
  Demultiplexer #(.select(2), .width(32)) demultiplexer_8 (
    .out0(demultiplexer_8_out0), .out1(demultiplexer_8_out1), .out2(demultiplexer_8_out2),
    .out3(demultiplexer_8_out3), .in(demultiplexer_6_out1), .sel(Write_Reg_num[3:2]));  // open: en
  Demultiplexer #(.select(2), .width(32)) demultiplexer_9 (
    .out0(W20), .out1(W21), .out2(W22), .out3(W23), .in(demultiplexer_8_out1), .sel(Write_Reg_num[1:0]));  // open: en
  Register #(.width(32)) register_21 (.D(W5), .en(Write_Enable), .Q(R5), .clk(Clock));  // open: clr
  Register #(.width(32)) register_22 (.D(W13), .en(Write_Enable), .Q(R13), .clk(Clock));  // open: clr
  Register #(.width(32)) register_23 (.D(W21), .en(Write_Enable), .Q(R21), .clk(Clock));  // open: clr
  Register #(.width(32)) register_24 (.D(W29), .en(Write_Enable), .Q(R29), .clk(Clock));  // open: clr
  Multiplexer #(.select(2), .width(32)) multiplexer_19 (
    .in0(R24), .in1(R25), .in2(R26), .in3(R27), .out(multiplexer_19_out), .sel(Reg1_num[1:0]));  // open: en
  Multiplexer #(.select(2), .width(32)) multiplexer_20 (
    .in0(R24), .in1(R25), .in2(R26), .in3(R27), .out(multiplexer_20_out), .sel(Reg2[1:0]));  // open: en
  Demultiplexer #(.select(2), .width(32)) demultiplexer_10 (
    .out0(W24), .out1(W25), .out2(W26), .out3(W27), .in(demultiplexer_8_out2), .sel(Write_Reg_num[1:0]));  // open: en
  Register #(.width(32)) register_25 (.D(W6), .en(Write_Enable), .Q(R6), .clk(Clock));  // open: clr
  Register #(.width(32)) register_26 (.D(W14), .en(Write_Enable), .Q(R14), .clk(Clock));  // open: clr
  Register #(.width(32)) register_27 (.D(W22), .en(Write_Enable), .Q(R22), .clk(Clock));  // open: clr
  Register #(.width(32)) register_28 (.D(W30), .en(Write_Enable), .Q(R30), .clk(Clock));  // open: clr
  Multiplexer #(.select(2), .width(32)) multiplexer_21 (
    .in0(R28), .in1(R29), .in2(R30), .in3(ra_Value), .out(multiplexer_21_out), .sel(Reg1_num[1:0]));  // open: en
  Multiplexer #(.select(2), .width(32)) multiplexer_22 (
    .in0(R28), .in1(R29), .in2(R30), .in3(ra_Value), .out(multiplexer_22_out), .sel(Reg2[1:0]));  // open: en
  Demultiplexer #(.select(2), .width(32)) demultiplexer_11 (
    .out0(W28), .out1(W29), .out2(W30), .out3(W31), .in(demultiplexer_8_out3), .sel(Write_Reg_num[1:0]));  // open: en
  Register #(.width(32)) register_29 (.D(W7), .en(Write_Enable), .Q(R7), .clk(Clock));  // open: clr
  Register #(.width(32)) register_30 (.D(W15), .en(Write_Enable), .Q(R15), .clk(Clock));  // open: clr
  Register #(.width(32)) register_31 (.D(W23), .en(Write_Enable), .Q(R23), .clk(Clock));  // open: clr
  Register #(.width(32)) register_32 (.D(W31), .en(Write_Enable), .Q(ra_Value), .clk(Clock));  // open: clr

  // Other names for the same wires on the sheet: clk = Clock; R16[31:0] = s0_Value; s0[31:0] = s0_Value;
  //   R17[31:0] = s1_Value; s1[31:0] = s1_Value; R18[31:0] = s2_Value; s2[31:0] = s2_Value; R31[31:0] = ra_Value;
  //   ra[31:0] = ra_Value; reg2_num[4:0] = Reg2; reg2_t[31:0] = Reg2_2; WE = Write_Enable; write_data[31:0] = Din

  // Notes on the sheet:
  //   输入引脚
  //   输出引脚
  //   Debug引脚，便于观测寄存器值
  //   请勿修改引脚以及封装，直接使用隧道连接电路
endmodule
