// Logisim project cpu多保存几份.circ as structural Verilog: 4 circuits, main circuit main
module main (
  input  in_1
);

  wire alu_1_equal, ALUSrc, and_2_out, and_3_out, beq, bne, clk, clock_1_out, comparator_1_eq, MemRead,
       MemWrite, not_1_out, not_2_out, or_1_out, or_2_out, PAUSE, RegWrite, \R型指令 , Shamt, Syscall, Unsigned,
       xnor_1_out;
  wire [1:0] Jmp, RegDst, toReg;
  wire [3:0] ALUop, register_2_q, register_2_q_3, register_2_q_4, register_2_q_5, register_2_q_6,
       register_2_q_7, register_2_q_8;
  wire [4:0] multiplexer_2_out;
  wire [7:4] register_2_q_2;
  wire [23:0] alu_1_result_2;
  wire [27:0] bit_extender_1_out, shifter_1_out;
  wire [31:0] a0, adder_2_out, alu_1_result, bit_extender_2_out, bit_extender_3_out, bit_extender_4_out,
       Itype, jaReg, Jtype, main_1_reg2_2, main_1_v0_value, multiplexer_3_out, multiplexer_4_out,
       multiplexer_5_out, multiplexer_6_out, multiplexer_7_out, multiplexer_8_out, PC, ram_1_data,
       register_1_q, rom_1_data, Rtype, shifter_2_out, total;

  Clock clock_1 (.out(clock_1_out));
  // Probe on multiplexer_7_out
  Multiplexer #(.enable("false")) multiplexer_1 (.in0(clock_1_out), .in1(1'b0), .out(clk), .sel(PAUSE));
  Counter #(.width(32), .max('hffffffff), .trigger("falling")) counter_1 (
    .load(1'b0), .count(1'b1), .Q(total), .clk(xnor_1_out));  // open: D, carry, clr
  // Probe on register_1_q
  Register #(.width(32)) register_1 (.D(multiplexer_7_out), .Q(register_1_q), .clk(clk));  // open: en, clr
  xnor xnor_1 (xnor_1_out, clk, PAUSE);
  Counter #(.width(32), .max('hffffffff), .trigger("falling")) counter_2 (
    .load(1'b0), .count(\R型指令 ), .Q(Rtype), .clk(xnor_1_out));  // open: D, carry, clr
  Adder #(.width(32)) adder_1 (.a(32'h4), .b(register_1_q), .out(PC));  // open: cin, cout
  // Probe on total
  // Probe on Rtype
  // Probe on Itype
  // Probe on Jtype
  or or_1 (or_1_out, ALUSrc, bne, beq);
  ROM #(.addrWidth(10), .dataWidth(32)) rom_1 (.addr(register_1_q[11:2]), .data(rom_1_data));  // open: sel
  Counter #(.width(32), .max('hffffffff), .trigger("falling")) counter_3 (
    .load(1'b0), .count(or_1_out), .Q(Itype), .clk(xnor_1_out));  // open: D, carry, clr
  assign bit_extender_1_out = {{2{rom_1_data[25]}}, rom_1_data[25:0]};  // Bit_Extender bit_extender_1
  \ALU控制  \alu控制_1  (
    .FUNCT(rom_1_data[5:0]), .OP(rom_1_data[31:26]), .alu_op(ALUop), .pause(Syscall), .jmp(Jmp),
    .alu_source(ALUSrc), .beq(beq), .bne(bne), .RegDes(RegDst), .RegWrite(RegWrite), .MemWrite(MemWrite),
    .toReg(toReg), .\R型指令 (\R型指令 ), .Unsigned(Unsigned), .shamt(Shamt), .MemRead(MemRead));
  // Probe on RegDst
  not not_1 (not_1_out, Jmp[0]);
  Shifter #(.width(28)) shifter_1 (.in(bit_extender_1_out), .\dist (5'b00010), .out(shifter_1_out));
  // Probe on rom_1_data[25:21]
  // Probe on rom_1_data[20:16]
  Multiplexer #(.select(2), .width(5), .enable("false")) multiplexer_2 (
    .in0(rom_1_data[20:16]), .in1(rom_1_data[15:11]), .in2({5{1'b1}}), .in3({5{1'b1}}),
    .out(multiplexer_2_out), .sel(RegDst));
  // Probe on multiplexer_2_out
  assign bit_extender_2_out = {{27{1'b0}}, rom_1_data[10:6]};  // Bit_Extender bit_extender_2
  assign bit_extender_3_out = {{16{rom_1_data[15]}}, rom_1_data[15:0]};  // Bit_Extender bit_extender_3
  Multiplexer #(.width(32), .enable("false")) multiplexer_3 (
    .in0(bit_extender_3_out), .in1(bit_extender_4_out), .out(multiplexer_3_out), .sel(Unsigned));
  assign bit_extender_4_out = {{16{1'b0}}, rom_1_data[15:0]};  // Bit_Extender bit_extender_4
  Counter #(.width(32), .max('hffffffff), .trigger("falling")) counter_4 (
    .load(1'b0), .count(not_1_out), .Q(Jtype), .clk(xnor_1_out));  // open: D, carry, clr
  Shifter #(.width(32)) shifter_2 (.in(multiplexer_3_out), .\dist (5'b00010), .out(shifter_2_out));
  Comparator #(.width(32)) comparator_1 (.a(32'ha), .b(main_1_v0_value), .eq(comparator_1_eq));  // open: gt, lt
  and and_1 (PAUSE, comparator_1_eq, Syscall);
  \ACM1401_U201414620_胡汉鹏_regfile_main  main_1 (
    .Reg1_num(rom_1_data[25:21]), .Reg2(rom_1_data[20:16]), .Write_Reg_num(multiplexer_2_out),
    .Din(multiplexer_8_out), .Write_Enable(RegWrite), .Clock(clk), .Reg1(jaReg), .Reg2_2(main_1_reg2_2),
    .v0_Value(main_1_v0_value), .a0_Value(a0));  // open: s2_Value, ra_Value
  // Probe on multiplexer_3_out
  // Probe on {PC[31:28], shifter_1_out}
  Multiplexer #(.width(32), .enable("false")) multiplexer_4 (
    .in0(PC), .in1(adder_2_out), .out(multiplexer_4_out), .sel(or_2_out));
  Adder #(.width(32)) adder_2 (.a(PC), .b(shifter_2_out), .out(adder_2_out));  // open: cin, cout
  or or_2 (or_2_out, and_2_out, and_3_out);
  and and_2 (and_2_out, bne, not_2_out);
  not not_2 (not_2_out, alu_1_equal);
  Multiplexer #(.width(32), .enable("false")) multiplexer_5 (
    .in0(jaReg), .in1(main_1_reg2_2), .out(multiplexer_5_out), .sel(Shamt));
  Multiplexer #(.select(2), .width(32), .enable("false")) multiplexer_6 (
    .in0(main_1_reg2_2), .in1(multiplexer_3_out), .in2(bit_extender_2_out), .in3(bit_extender_2_out),
    .out(multiplexer_6_out), .sel({Shamt, ALUSrc}));
  // Probe on multiplexer_8_out
  Hex_Digit_Display hex_digit_display_1 (.value(register_2_q_8));  // open: dp
  and and_3 (and_3_out, beq, alu_1_equal);
  ALU alu_1 (
    .AluOP(ALUop), .X(multiplexer_5_out), .Equal(alu_1_equal),
    .Result({alu_1_result[31:26], alu_1_result_2, alu_1_result[1:0]}), .Y(multiplexer_6_out));  // open: Signed_Overflow, Result_2, UnSigned_Overflow
  Hex_Digit_Display hex_digit_display_2 (.value(register_2_q_7));  // open: dp
  Hex_Digit_Display hex_digit_display_3 (.value(register_2_q_6));  // open: dp
  Register #(.width(32)) register_2 (
    .D(a0),
    .Q({register_2_q_8, register_2_q_7, register_2_q_6, register_2_q_5, register_2_q_4, register_2_q_3, register_2_q_2, register_2_q}),
    .clk(Syscall));  // open: en, clr
  // Probe on main_1_reg2_2
  Multiplexer #(.select(2), .width(32), .enable("false")) multiplexer_7 (
    .in0({PC[31:28], shifter_1_out}), .in1(multiplexer_4_out), .in2(jaReg), .in3(jaReg),
    .out(multiplexer_7_out), .sel(Jmp));
  // Probe on Jmp
  Hex_Digit_Display hex_digit_display_4 (.value(register_2_q_4));  // open: dp
  Hex_Digit_Display hex_digit_display_5 (.value(register_2_q_5));  // open: dp
  // Probe on {alu_1_result[31:26], alu_1_result_2, alu_1_result[1:0]}
  Hex_Digit_Display hex_digit_display_6 (.value(register_2_q_3));  // open: dp
  Hex_Digit_Display hex_digit_display_7 (.value(register_2_q_2));  // open: dp
  RAM #(.addrWidth(24), .dataWidth(32), .bus("separate")) ram_1 (
    .addr(alu_1_result_2), .din(main_1_reg2_2), .data(ram_1_data), .str(MemWrite), .clk(clk), .ld(MemRead),
    .clr(in_1));  // open: sel
  Hex_Digit_Display hex_digit_display_8 (.value(register_2_q));  // open: dp
  Multiplexer #(.select(2), .width(32), .enable("false")) multiplexer_8 (
    .in0({alu_1_result[31:26], alu_1_result_2, alu_1_result[1:0]}), .in1(ram_1_data), .in2(PC), .in3(PC),
    .out(multiplexer_8_out), .sel(toReg));
  // Probe on toReg

  // Other names for the same wires on the sheet: 清零 = in_1

  // Notes on the sheet:
  //   rs
  //   rt
  //   rd
  //   contents of rom_1 (hex, n*v repeats v):
  //   20110001 8000c05 20110001 20120002 20130003 8000c09 20110001 20120002 20130003 8000c0d 20110001
  //   20120002 20130003 8000c11 20110001 20120002 20130003 c000cb8 20100001 20110001 118fc0 112020
  //   20020022 c 118882 12200001 8000c15 112020 20020022 c 20110001 118880 112020 20020022 c 12200001
  //   8000c1f 20110001 118fc0 112020 20020022 c 1188c3 112020 20020022 c 118903 112020 20020022 c 118903
  //   112020 20020022 c 118903 112020 20020022 c 118903 112020 20020022 c 118903 112020 20020022 c 118903
  //   112020 20020022 c 118903 112020 20020022 c 20100001 109fc0 139fc3 8021 2012000c 24160003 26100001
  //   3210000f 20080008 20090001 139900 2709825 132020 20020022 c 1094022 1500fff9 22100001 2018000f
  //   2188024 108700 20080008 20090001 139902 2709825 132021 20020022 c 1094022 1500fff9 108702 2c9b022
  //   12c00001 8000c50 4020 1084027 84400 3508ffff 82021 20020022 c 2010ffff 20110000 ae300000 22100001
  //   22310004 ae300000 22100001 22310004 ae300000 22100001 22310004 ae300000 22100001 22310004 ae300000
  //   22100001 22310004 ae300000 22100001 22310004 ae300000 22100001 22310004 ae300000 22100001 22310004
  //   ae300000 22100001 22310004 ae300000 22100001 22310004 ae300000 22100001 22310004 ae300000 22100001
  //   22310004 ae300000 22100001 22310004 ae300000 22100001 22310004 ae300000 22100001 22310004 ae300000
  //   22100001 22310004 22100001 8020 2011003c 8e130000 8e340000 274402a 11000002 ae330000 ae140000
  //   2231fffc 1611fff8 102020 20020022 c 22100004 2011003c 1611fff2 2002000a c 20100000 22100001 102020
  //   20020022 c 22100002 102020 20020022 c 22100003 102020 20020022 c 22100004 102020 20020022 c 22100005
  //   102020 20020022 c 22100006 102020 20020022 c 22100007 102020 20020022 c 22100008 102020 20020022
  //   20020022 c 3e00008
  //   shamt
  //   immediate
endmodule

// 控制器
module \ALU控制  (
  input  [5:0] FUNCT,
  input  [5:0] OP,
  output MemWrite,
  output [1:0] RegDes,
  output MemRead,
  output [1:0] toReg,
  output alu_source,
  output \R型指令 ,
  output RegWrite,
  output [3:0] alu_op,
  output pause,
  output [1:0] jmp,
  output bne,
  output beq,
  output shamt,
  output Unsigned
);

  wire or_2_out, or_3_out, or_5_out, or_9_out, or_10_out, or_11_out, trans_1_i1, trans_1_i1_2, trans_1_i2_2,
       trans_1_i3_2, trans_1_i4_2, trans_1_i5_2, trans_1_i6, trans_1_i6_2, trans_1_i7, trans_1_i7_2,
       trans_1_i8, trans_1_i8_2, trans_1_i9, trans_1_i9_2, trans_1_i10_2, trans_1_i11_2, trans_1_i12_2;
  wire [3:0] multiplexer_1_out, multiplexer_2_out, multiplexer_3_out, multiplexer_4_out, multiplexer_5_out,
       multiplexer_6_out, multiplexer_7_out, multiplexer_9_out, multiplexer_10_out;

  trans trans_1 (
    .a0(FUNCT[0]), .a1(FUNCT[1]), .a2(FUNCT[2]), .a3(FUNCT[3]), .a4(FUNCT[4]), .a5(FUNCT[5]), .a6(OP[0]),
    .a7(OP[1]), .a8(OP[2]), .a9(OP[3]), .a10(OP[4]), .a11(OP[5]), .i1_2(trans_1_i1_2), .i2(MemRead),
    .i3(MemWrite), .i4(beq), .i5(bne), .i6(trans_1_i6), .i7(trans_1_i7), .i8(trans_1_i8), .i9(trans_1_i9),
    .i10(RegDes[1]), .i11(jmp[1]), .i12(pause), .i1(trans_1_i1), .i2_2(trans_1_i2_2), .i3_2(trans_1_i3_2),
    .i4_2(trans_1_i4_2), .i5_2(trans_1_i5_2), .i6_2(trans_1_i6_2), .i7_2(trans_1_i7_2), .i8_2(trans_1_i8_2),
    .i9_2(trans_1_i9_2), .i10_2(trans_1_i10_2), .i11_2(trans_1_i11_2), .i12_2(trans_1_i12_2));
  or or_1 (alu_source, MemWrite, or_2_out);
  or or_2 (or_2_out, MemRead, trans_1_i2_2, trans_1_i3_2, trans_1_i6_2, trans_1_i12_2, trans_1_i7);
  nor nor_1 (jmp[0], RegDes[1], trans_1_i9);
  not not_1 (RegDes[0], alu_source);
  or or_3 (or_3_out, trans_1_i7, trans_1_i6);
  or or_4 (RegWrite, or_2_out, or_5_out, RegDes[1]);
  or or_5 (or_5_out, trans_1_i1, trans_1_i4_2, trans_1_i5_2, trans_1_i7_2, trans_1_i8_2, trans_1_i9_2, trans_1_i10_2, trans_1_i11_2, trans_1_i1_2, trans_1_i6, trans_1_i8);
  or or_6 (Unsigned, trans_1_i3_2, trans_1_i4_2, trans_1_i6_2, trans_1_i12_2, trans_1_i8);
  or or_7 (\R型指令 , or_5_out, jmp[1], pause);
  or or_8 (shamt, trans_1_i7_2, trans_1_i8_2, trans_1_i9_2);
  or or_9 (or_9_out, trans_1_i1, trans_1_i2_2, trans_1_i3_2, trans_1_i4_2);
  or or_10 (or_10_out, trans_1_i5_2, trans_1_i6_2);
  or or_11 (or_11_out, trans_1_i11_2, trans_1_i12_2);
  Multiplexer #(.width(4), .enable("false")) multiplexer_1 (
    .in0(multiplexer_2_out), .in1(4'b1000), .out(multiplexer_1_out), .sel(or_11_out));
  Multiplexer #(.width(4), .enable("false")) multiplexer_2 (
    .in0(multiplexer_3_out), .in1(4'b1010), .out(multiplexer_2_out), .sel(trans_1_i1_2));
  Multiplexer #(.width(4), .enable("false")) multiplexer_3 (
    .in0(multiplexer_4_out), .in1(4'b1011), .out(multiplexer_3_out), .sel(or_3_out));
  Multiplexer #(.width(4), .enable("false")) multiplexer_4 (
    .in0(4'b0101), .in1(4'b1100), .out(multiplexer_4_out), .sel(trans_1_i8));
  Multiplexer #(.width(4), .enable("false")) multiplexer_5 (
    .in0(multiplexer_6_out), .in1(4'b0001), .out(multiplexer_5_out), .sel(trans_1_i8_2));
  Multiplexer #(.width(4), .enable("false")) multiplexer_6 (
    .in0(multiplexer_7_out), .in1(4'b0010), .out(multiplexer_6_out), .sel(trans_1_i9_2));
  Multiplexer #(.width(4), .enable("false")) multiplexer_7 (
    .in0(multiplexer_1_out), .in1(4'b0110), .out(multiplexer_7_out), .sel(trans_1_i10_2));
  Multiplexer #(.width(4), .enable("false")) multiplexer_8 (
    .in0(multiplexer_9_out), .in1(4'b0101), .out(alu_op), .sel(or_9_out));
  Multiplexer #(.width(4), .enable("false")) multiplexer_9 (
    .in0(multiplexer_10_out), .in1(4'b0111), .out(multiplexer_9_out), .sel(or_10_out));
  Multiplexer #(.width(4), .enable("false")) multiplexer_10 (
    .in0(multiplexer_5_out), .in1(4'b0000), .out(multiplexer_10_out), .sel(trans_1_i7_2));

  assign toReg = {RegDes[1], MemRead};

  // Other names for the same wires on the sheet: jal = RegDes[1]
endmodule

module controler (
  input  op1,
  input  OP2,
  input  OP3,
  input  [5:0] FUNCT,
  input  OP4,
  input  OP5,
  input  [5:0] OP,
  input  OP6,
  output RegDst,
  output out_10,
  output out_11,
  output out_12,
  output [3:0] out_13,
  output Branch1,
  output [1:0] out_15,
  output out_16,
  output Bracnch,
  output out_18,
  output out_19,
  output out_20,
  output Jump,
  output [1:0] out_22,
  output out_23,
  output MemtoReg,
  output out_25,
  output out_26,
  output out_27,
  output MemRead,
  output out_29,
  output [1:0] out_30,
  output MemWrite,
  output out_32,
  output out_33,
  output out_34,
  output out_35,
  output out_36,
  output ALUSrc,
  output out_38,
  output out_39,
  output out_40,
  output out_41,
  output out_42,
  output ALUop,
  output out_44,
  output out_45,
  output out_46,
  output out_47,
  output out_48,
  output out_49,
  output out_50,
  output out_51,
  output RegWrite,
  output out_53,
  output out_54,
  output out_55,
  output out_56,
  output out_57,
  output out_58
);

  wire ALUSrc_t, and_7_out, and_8_out, beq, bne, \I型指令 , jal, jr, \J型指令 , MemRead_t, MemWrite_t, not_1_out,
       not_2_out, not_3_out, not_4_out, not_5_out, not_6_out, not_7_out, not_9_out, not_10_out, not_11_out,
       not_12_out, RegWrite_t, \R型指令 , Syscall;
  wire [1:0] Jmp, RegDst_t, toReg;
  wire [3:0] ALUop_t;

  not not_1 (not_1_out, OP3);
  not not_2 (not_2_out, OP4);
  not not_3 (not_3_out, OP5);
  not not_4 (not_4_out, OP5);
  not not_5 (not_5_out, OP6);
  not not_6 (not_6_out, OP3);
  not not_7 (not_7_out, OP3);
  and and_1 (MemWrite, op1, OP3);
  or or_1 (ALUSrc, OP5, OP3);
  not not_8 (ALUop, OP4);
  not not_9 (not_9_out, OP3);
  not not_10 (not_10_out, OP4);
  not not_11 (not_11_out, OP4);
  not not_12 (not_12_out, OP5);
  and and_2 (RegDst, not_1_out, not_2_out, not_3_out);
  and and_3 (Branch1, not_4_out, OP6);
  and and_4 (Bracnch, OP4, not_5_out);
  and and_5 (MemtoReg, op1, not_6_out);
  and and_6 (MemRead, op1, not_7_out);
  and and_7 (and_7_out, not_9_out, not_10_out);
  and and_8 (and_8_out, not_11_out, not_12_out);
  or or_2 (RegWrite, and_7_out, and_8_out);
  // ALU控制 alu控制_1: pin names not known; wires that end beside it: FUNCT, OP, out_10, out_11, out_12, out_13, out_15, out_16, out_18, out_19, out_20, out_22, out_23, out_25, out_26, out_27, out_29, out_30, \R型指令 , \I型指令 , \J型指令 , ALUop_t, Jmp, Syscall, ALUSrc_t, beq, bne, RegDst_t, RegWrite_t, MemWrite_t, MemRead_t, jal, jr, toReg
  trans trans_1 (
    .a0(FUNCT[0]), .a1(FUNCT[1]), .a2(FUNCT[2]), .a3(FUNCT[3]), .a4(FUNCT[4]), .a5(FUNCT[5]), .a6(OP[0]),
    .a7(OP[1]), .a8(OP[2]), .a9(OP[3]), .a10(OP[4]), .a11(OP[5]), .i1_2(out_46), .i2(out_47), .i3(out_48),
    .i4(out_49), .i5(out_50), .i6(out_51), .i7(out_53), .i8(out_54), .i9(out_55), .i10(out_56), .i11(out_57),
    .i12(out_58), .i1(out_32), .i2_2(out_33), .i3_2(out_34), .i4_2(out_35), .i5_2(out_36), .i6_2(out_38),
    .i7_2(out_39), .i8_2(out_40), .i9_2(out_41), .i10_2(out_42), .i11_2(out_44), .i12_2(out_45));

  assign Jump = 1'b0;
endmodule

module trans (
  input  a0,
  input  a1,
  input  a2,
  input  a3,
  input  a4,
  input  a5,
  input  a6,
  input  a7,
  input  a8,
  input  a9,
  input  a10,
  input  a11,
  output i1,
  output i1_2,
  output i2,
  output i2_2,
  output i3,
  output i3_2,
  output i4,
  output i5,
  output i4_2,
  output i6,
  output i5_2,
  output i7,
  output i6_2,
  output i8,
  output i7_2,
  output i9,
  output i10,
  output i8_2,
  output i11,
  output i9_2,
  output i12,
  output i10_2,
  output i11_2,
  output i12_2
);

  wire not_1_out, not_2_out, not_3_out, not_4_out, not_5_out, not_6_out, not_7_out, not_8_out, not_9_out,
       not_10_out, not_11_out, not_12_out, not_13_out, not_14_out, not_15_out, not_16_out, not_17_out,
       not_18_out, not_19_out, not_20_out, not_21_out, not_22_out, not_23_out, not_24_out, not_25_out,
       not_26_out, not_27_out, not_28_out, not_29_out, not_30_out, not_31_out, not_32_out, not_33_out,
       not_34_out, not_35_out, not_36_out, not_37_out, not_38_out, not_39_out, not_40_out, not_41_out,
       not_42_out, not_43_out, not_44_out, not_45_out, not_46_out, not_47_out, not_48_out, not_49_out,
       not_50_out, not_51_out, not_52_out, not_53_out, not_54_out, not_55_out, not_56_out, not_57_out,
       not_58_out, not_59_out, not_60_out, not_61_out, not_62_out, not_63_out, not_64_out, not_65_out,
       not_66_out, not_67_out, not_68_out, not_69_out, not_70_out, not_71_out, not_72_out, not_73_out,
       not_74_out, not_75_out, not_76_out, not_77_out, not_78_out, not_79_out, not_80_out, not_81_out,
       not_82_out, not_83_out, not_84_out, not_85_out, not_86_out, not_87_out, not_88_out, not_89_out,
       not_90_out, not_91_out, not_92_out, not_93_out, not_94_out, not_95_out, not_96_out, not_97_out,
       not_98_out, not_99_out, not_100_out, not_101_out, not_102_out, not_103_out, not_104_out, not_105_out,
       not_106_out, not_107_out, not_108_out, not_109_out, not_110_out, not_111_out, not_112_out,
       not_113_out, not_114_out, not_115_out, not_116_out, not_117_out, not_118_out, not_119_out,
       not_120_out, not_121_out, not_122_out, not_123_out, not_124_out, not_125_out, not_126_out,
       not_127_out, not_128_out, not_129_out, not_130_out, not_131_out, not_132_out, not_133_out,
       not_134_out, not_135_out, not_136_out, not_137_out, not_138_out, not_139_out, not_140_out,
       not_141_out, not_142_out, not_143_out, not_144_out, not_145_out, not_146_out, not_147_out,
       not_148_out, not_149_out, not_150_out, not_151_out, not_152_out, not_153_out, not_154_out,
       not_155_out, not_156_out, not_157_out, not_158_out, not_159_out, not_160_out, not_161_out,
       not_162_out, not_163_out, not_164_out, not_165_out, not_166_out, not_167_out, not_168_out,
       not_169_out, not_170_out, not_171_out, not_172_out;

  not not_1 (not_1_out, a11);
  not not_2 (not_2_out, a10);
  not not_3 (not_3_out, a9);
  not not_4 (not_4_out, a8);
  not not_5 (not_5_out, a7);
  not not_6 (not_6_out, a6);
  not not_7 (not_7_out, a4);
  not not_8 (not_8_out, a3);
  not not_9 (not_9_out, a2);
  not not_10 (not_10_out, a1);
  not not_11 (not_11_out, a0);
  not not_12 (not_12_out, a11);
  not not_13 (not_13_out, a10);
  not not_14 (not_14_out, a8);
  not not_15 (not_15_out, a7);
  not not_16 (not_16_out, a6);
  not not_17 (not_17_out, a11);
  not not_18 (not_18_out, a10);
  not not_19 (not_19_out, a8);
  not not_20 (not_20_out, a7);
  not not_21 (not_21_out, a11);
  not not_22 (not_22_out, a10);
  not not_23 (not_23_out, a9);
  not not_24 (not_24_out, a8);
  not not_25 (not_25_out, a7);
  not not_26 (not_26_out, a6);
  not not_27 (not_27_out, a4);
  not not_28 (not_28_out, a3);
  not not_29 (not_29_out, a2);
  not not_30 (not_30_out, a1);
  not not_31 (not_31_out, a11);
  not not_32 (not_32_out, a10);
  not not_33 (not_33_out, a9);
  not not_34 (not_34_out, a8);
  not not_35 (not_35_out, a7);
  not not_36 (not_36_out, a6);
  not not_37 (not_37_out, a4);
  not not_38 (not_38_out, a3);
  not not_39 (not_39_out, a1);
  not not_40 (not_40_out, a0);
  not not_41 (not_41_out, a11);
  not not_42 (not_42_out, a10);
  not not_43 (not_43_out, a7);
  not not_44 (not_44_out, a6);
  not not_45 (not_45_out, a11);
  not not_46 (not_46_out, a10);
  not not_47 (not_47_out, a9);
  not not_48 (not_48_out, a8);
  not not_49 (not_49_out, a7);
  not not_50 (not_50_out, a6);
  not not_51 (not_51_out, a5);
  not not_52 (not_52_out, a4);
  not not_53 (not_53_out, a3);
  not not_54 (not_54_out, a2);
  not not_55 (not_55_out, a1);
  not not_56 (not_56_out, a0);
  not not_57 (not_57_out, a11);
  not not_58 (not_58_out, a10);
  not not_59 (not_59_out, a9);
  not not_60 (not_60_out, a8);
  not not_61 (not_61_out, a7);
  not not_62 (not_62_out, a6);
  not not_63 (not_63_out, a5);
  not not_64 (not_64_out, a4);
  not not_65 (not_65_out, a3);
  not not_66 (not_66_out, a2);
  not not_67 (not_67_out, a11);
  not not_68 (not_68_out, a10);
  not not_69 (not_69_out, a9);
  not not_70 (not_70_out, a8);
  not not_71 (not_71_out, a7);
  not not_72 (not_72_out, a6);
  not not_73 (not_73_out, a5);
  not not_74 (not_74_out, a4);
  not not_75 (not_75_out, a3);
  not not_76 (not_76_out, a2);
  not not_77 (not_77_out, a0);
  not not_78 (not_78_out, a11);
  not not_79 (not_79_out, a10);
  not not_80 (not_80_out, a9);
  not not_81 (not_81_out, a8);
  not not_82 (not_82_out, a7);
  not not_83 (not_83_out, a6);
  not not_84 (not_84_out, a4);
  not not_85 (not_85_out, a3);
  not not_86 (not_86_out, a2);
  not not_87 (not_87_out, a0);
  not not_88 (not_88_out, a11);
  not not_89 (not_89_out, a10);
  not not_90 (not_90_out, a9);
  not not_91 (not_91_out, a8);
  not not_92 (not_92_out, a7);
  not not_93 (not_93_out, a6);
  not not_94 (not_94_out, a4);
  not not_95 (not_95_out, a3);
  not not_96 (not_96_out, a1);
  not not_97 (not_97_out, a11);
  not not_98 (not_98_out, a10);
  not not_99 (not_99_out, a7);
  and and_1 (i1, not_1_out, not_2_out, not_3_out, not_4_out, not_5_out, not_6_out, a5, not_7_out, not_8_out, not_9_out, not_10_out, not_11_out);
  and and_2 (i2_2, not_12_out, not_13_out, a9, not_14_out, not_15_out, not_16_out);
  and and_3 (i3_2, not_17_out, not_18_out, a9, not_19_out, not_20_out, a6);
  and and_4 (i4_2, not_21_out, not_22_out, not_23_out, not_24_out, not_25_out, not_26_out, a5, not_27_out, not_28_out, not_29_out, not_30_out, a0);
  and and_5 (i5_2, not_31_out, not_32_out, not_33_out, not_34_out, not_35_out, not_36_out, a5, not_37_out, not_38_out, a2, not_39_out, not_40_out);
  and and_6 (i6_2, not_41_out, not_42_out, a9, a8, not_43_out, not_44_out);
  and and_7 (i7_2, not_45_out, not_46_out, not_47_out, not_48_out, not_49_out, not_50_out, not_51_out, not_52_out, not_53_out, not_54_out, not_55_out, not_56_out);
  and and_8 (i8_2, not_57_out, not_58_out, not_59_out, not_60_out, not_61_out, not_62_out, not_63_out, not_64_out, not_65_out, not_66_out, a1, a0);
  and and_9 (i9_2, not_67_out, not_68_out, not_69_out, not_70_out, not_71_out, not_72_out, not_73_out, not_74_out, not_75_out, not_76_out, a1, not_77_out);
  and and_10 (i10_2, not_78_out, not_79_out, not_80_out, not_81_out, not_82_out, not_83_out, a5, not_84_out, not_85_out, not_86_out, a1, not_87_out);
  and and_11 (i11_2, not_88_out, not_89_out, not_90_out, not_91_out, not_92_out, not_93_out, a5, not_94_out, not_95_out, a2, not_96_out, a0);
  and and_12 (i12_2, not_97_out, not_98_out, a9, a8, not_99_out, a6);
  not not_100 (not_100_out, a11);
  not not_101 (not_101_out, a10);
  not not_102 (not_102_out, a9);
  not not_103 (not_103_out, a8);
  not not_104 (not_104_out, a7);
  not not_105 (not_105_out, a6);
  not not_106 (not_106_out, a4);
  not not_107 (not_107_out, a3);
  not not_108 (not_108_out, a10);
  not not_109 (not_109_out, a9);
  not not_110 (not_110_out, a8);
  not not_111 (not_111_out, a10);
  not not_112 (not_112_out, a8);
  not not_113 (not_113_out, a11);
  not not_114 (not_114_out, a10);
  not not_115 (not_115_out, a9);
  not not_116 (not_116_out, a7);
  not not_117 (not_117_out, a6);
  not not_118 (not_118_out, a11);
  not not_119 (not_119_out, a10);
  not not_120 (not_120_out, a9);
  not not_121 (not_121_out, a7);
  not not_122 (not_122_out, a11);
  not not_123 (not_123_out, a10);
  not not_124 (not_124_out, a9);
  not not_125 (not_125_out, a8);
  not not_126 (not_126_out, a7);
  not not_127 (not_127_out, a6);
  not not_128 (not_128_out, a4);
  not not_129 (not_129_out, a2);
  not not_130 (not_130_out, a0);
  not not_131 (not_131_out, a11);
  not not_132 (not_132_out, a10);
  not not_133 (not_133_out, a8);
  not not_134 (not_134_out, a6);
  not not_135 (not_135_out, a11);
  not not_136 (not_136_out, a10);
  not not_137 (not_137_out, a9);
  not not_138 (not_138_out, a8);
  not not_139 (not_139_out, a7);
  not not_140 (not_140_out, a6);
  not not_141 (not_141_out, a4);
  not not_142 (not_142_out, a2);
  not not_143 (not_143_out, a11);
  not not_144 (not_144_out, a10);
  not not_145 (not_145_out, a9);
  not not_146 (not_146_out, a8);
  not not_147 (not_147_out, a6);
  not not_148 (not_148_out, a11);
  not not_149 (not_149_out, a10);
  not not_150 (not_150_out, a9);
  not not_151 (not_151_out, a8);
  not not_152 (not_152_out, a11);
  not not_153 (not_153_out, a10);
  not not_154 (not_154_out, a9);
  not not_155 (not_155_out, a8);
  not not_156 (not_156_out, a7);
  not not_157 (not_157_out, a6);
  not not_158 (not_158_out, a5);
  not not_159 (not_159_out, a4);
  not not_160 (not_160_out, a2);
  not not_161 (not_161_out, a1);
  not not_162 (not_162_out, a0);
  not not_163 (not_163_out, a11);
  not not_164 (not_164_out, a10);
  not not_165 (not_165_out, a9);
  not not_166 (not_166_out, a8);
  not not_167 (not_167_out, a7);
  not not_168 (not_168_out, a6);
  not not_169 (not_169_out, a5);
  not not_170 (not_170_out, a4);
  not not_171 (not_171_out, a1);
  not not_172 (not_172_out, a0);
  and and_13 (i1_2, not_100_out, not_101_out, not_102_out, not_103_out, not_104_out, not_105_out, a5, not_106_out, not_107_out, a2, a1, a0);
  and and_14 (i2, a11, not_108_out, not_109_out, not_110_out, a7, a6);
  and and_15 (i3, a11, not_111_out, a9, not_112_out, a7, a6);
  and and_16 (i4, not_113_out, not_114_out, not_115_out, a8, not_116_out, not_117_out);
  and and_17 (i5, not_118_out, not_119_out, not_120_out, a8, not_121_out, a6);
  and and_18 (i6, not_122_out, not_123_out, not_124_out, not_125_out, not_126_out, not_127_out, a5, not_128_out, a3, not_129_out, a1, not_130_out);
  and and_19 (i7, not_131_out, not_132_out, a9, not_133_out, a7, not_134_out);
  and and_20 (i8, not_135_out, not_136_out, not_137_out, not_138_out, not_139_out, not_140_out, a5, not_141_out, a3, not_142_out, a1, a0);
  and and_21 (i9, not_143_out, not_144_out, not_145_out, not_146_out, a7, not_147_out);
  and and_22 (i10, not_148_out, not_149_out, not_150_out, not_151_out, a7, a6);
  and and_23 (i11, not_152_out, not_153_out, not_154_out, not_155_out, not_156_out, not_157_out, not_158_out, not_159_out, a3, not_160_out, not_161_out, not_162_out);
  and and_24 (i12, not_163_out, not_164_out, not_165_out, not_166_out, not_167_out, not_168_out, not_169_out, not_170_out, a3, a2, not_171_out, not_172_out);
endmodule
