// Logisim project cpu2.1.circ as structural Verilog: 13 circuits, main circuit main
module main (
  input  in_1
);

  wire \_1号中断_out , \_2号中断_out , \_3号中断_out , alu_1_equal, ALUSrc, and_3_out, and_4_out, and_5_out, beq,
       BGEZ, bgez_t, bne, clk, comparator_1_eq, comparator_2_eq, eret, ex_mem_1_mfc0_out,
       ex_mem_1_mfc0_out_2, ex_mem_1_regwrite_out, id_ex_1_lh_out, id_ex_1_memread_out, id_ex_1_memwrite_out,
       id_ex_1_mfc0_out, id_ex_1_mtc0_out, id_ex_1_regwrite_out, \ir_1__1号中断等待 , \ir_1__2号中断等待 ,
       \ir_1__3号中断等待 , jal, jr, lh, MemRead, MemWrite, mfc0, mtc0, not_1_out, not_2_out, not_3_out, or_1_out,
       or_2_out, or_3_out, PAUSE, RegWrite, \R型指令 , Shamt, srav, Syscall, trap, Unsigned, xnor_1_out;
  wire [1:0] ex_mem_1_regdst_out, ex_mem_1_toreg_out, id_ex_1_regdst_out, id_ex_1_toreg_out, ir_1_ir_no, Jmp,
       RegDst, toReg;
  wire [3:0] ALUop, register_2_q_2, register_2_q_3, register_2_q_4, register_2_q_5;
  wire [4:0] multiplexer_3_out, multiplexer_4_out, multiplexer_5_out, rd, rt;
  wire [15:0] multiplexer_15_out, register_2_q;
  wire [27:0] bit_extender_1_out, shifter_1_out;
  wire [31:0] a0, adder_2_out, alu_1_result, bit_extender_2_out, bit_extender_3_out, bit_extender_4_out,
       bit_extender_5_out, bit_extender_6_out, cp0_epc, cp0_no1, cp0_R1, cpc, ex_mem_1_aluresult_out,
       ex_mem_1_pc_out, ex_mem_1_r1_out, id_ex_1_immediate_out, id_ex_1_pc_out, id_ex_1_r1_out,
       id_ex_1_shamt_out_2, if_id_1_ir_out, if_id_1_pc_out, Itype, jaReg, Jtype, main_1_reg1, main_1_reg2_2,
       main_1_v0_value, mem_wb_1_aluresult_out, mem_wb_1_memdata_out, mem_wb_1_pc_out, multiplexer_2_out,
       multiplexer_6_out, multiplexer_7_out, multiplexer_8_out, multiplexer_9_out, multiplexer_10_out,
       multiplexer_11_out, multiplexer_12_out, multiplexer_13_out, multiplexer_14_out, multiplexer_16_out,
       multiplexer_17_out, multiplexer_18_out, npc, PC, ram_1_data, rom_1_data, rom_2_data, Rtype,
       shifter_2_out, sp, total;

  Clock clock_1 (.out(clk));
  // Probe on multiplexer_14_out
  Register #(.width(32)) register_1 (.D(multiplexer_14_out), .en(not_1_out), .Q(npc), .clk(clk));  // open: clr
  not not_1 (not_1_out, PAUSE);
  Counter #(.width(32), .max('hffffffff), .trigger("falling")) counter_1 (
    .load(1'b0), .count(1'b1), .Q(total), .clk(xnor_1_out));  // open: D, carry, clr
  // Probe on cpc
  Multiplexer #(.width(32), .enable("false")) multiplexer_1 (.in0(npc), .in1(32'h80000000), .out(cpc), .sel(trap));
  Counter #(.width(32), .max('hffffffff), .trigger("falling")) counter_2 (
    .load(1'b0), .count(\R型指令 ), .Q(Rtype), .clk(xnor_1_out));  // open: D, carry, clr
  xnor xnor_1 (xnor_1_out, clk, PAUSE);
  Adder #(.width(32)) adder_1 (.a(32'h4), .b(cpc), .out(PC));  // open: cin, cout
  // Probe on cpc
  Counter #(.width(32), .max('hffffffff), .trigger("falling")) counter_3 (
    .load(1'b0), .count(or_1_out), .Q(Itype), .clk(xnor_1_out));  // open: D, carry, clr
  or or_1 (or_1_out, ALUSrc, bne, beq, bgez_t);
  ROM #(.addrWidth(10), .dataWidth(32)) rom_1 (.addr(cpc[11:2]), .data(rom_1_data));  // open: sel
  ROM #(.addrWidth(10), .dataWidth(32)) rom_2 (.addr(cpc[11:2]), .data(rom_2_data));  // open: sel
  Multiplexer #(.width(32), .enable("false")) multiplexer_2 (
    .in0(rom_1_data), .in1(rom_2_data), .out(multiplexer_2_out), .sel(cpc[31]));
  Counter #(.width(32), .max('hffffffff), .trigger("falling")) counter_4 (
    .load(1'b0), .count(not_2_out), .Q(Jtype), .clk(xnor_1_out));  // open: D, carry, clr
  not not_2 (not_2_out, Jmp[0]);
  IF_ID if_id_1 (
    .pc_in(PC), .ir_in(multiplexer_2_out), .clk(clk), .pc_out(if_id_1_pc_out),
    .ir_out({if_id_1_ir_out[31:21], rt, rd, if_id_1_ir_out[10:0]}));
  // Probe on {if_id_1_ir_out[31:21], rt, rd, if_id_1_ir_out[10:0]}
  Hex_Digit_Display hex_digit_display_1 (.value(register_2_q_5));  // open: dp
  // Probe on a0
  assign bit_extender_1_out = {{2{if_id_1_ir_out[25]}}, {if_id_1_ir_out[25:21], rt, rd, if_id_1_ir_out[10:0]}};  // Bit_Extender bit_extender_1
  cpo_instru cpo_instru_1 (
    .in_1({if_id_1_ir_out[31:21], rt, rd, if_id_1_ir_out[10:0]}), .out_2(eret), .out_3(mfc0), .out_4(mtc0));
  Hex_Digit_Display hex_digit_display_2 (.value(register_2_q_3));  // open: dp
  Hex_Digit_Display hex_digit_display_3 (.value(register_2_q_4));  // open: dp
  Register #(.width(32)) register_2 (
    .D(a0), .Q({register_2_q_5, register_2_q_4, register_2_q_3, register_2_q_2, register_2_q}), .clk(Syscall));  // open: en, clr
  Shifter #(.width(28)) shifter_1 (.in(bit_extender_1_out), .\dist (5'b00010), .out(shifter_1_out));
  and and_1 (BGEZ, bgez_t, comparator_1_eq);
  Comparator #(.width(5)) comparator_1 (.a(5'b00001), .b(rt), .eq(comparator_1_eq));  // open: gt, lt
  // Probe on if_id_1_ir_out[25:21]
  Multiplexer #(.width(5), .enable("false")) multiplexer_3 (
    .in0(rt), .in1({5{1'b1}}), .out(multiplexer_3_out), .sel(jr));
  // Probe on multiplexer_3_out
  Multiplexer #(.select(2), .width(5), .enable("false")) multiplexer_4 (
    .in0(rt), .in1(rd), .in2({5{1'b1}}), .in3({5{1'b1}}), .out(multiplexer_4_out), .sel(RegDst));
  // Probe on RegDst
  assign bit_extender_2_out = {{27{1'b0}}, if_id_1_ir_out[10:6]};  // Bit_Extender bit_extender_2
  assign bit_extender_3_out = {{16{rd[4]}}, {rd, if_id_1_ir_out[10:0]}};  // Bit_Extender bit_extender_3
  assign bit_extender_4_out = {{16{1'b0}}, {rd, if_id_1_ir_out[10:0]}};  // Bit_Extender bit_extender_4
  Hex_Digit_Display hex_digit_display_4 (.value(register_2_q_2));  // open: dp
  Hex_Digit_Display hex_digit_display_5 (.value(register_2_q[15:12]));  // open: dp
  // Probe on multiplexer_5_out
  Multiplexer #(.width(5), .enable("false")) multiplexer_5 (
    .in0(multiplexer_4_out), .in1(rt), .out(multiplexer_5_out), .sel(mfc0));
  Multiplexer #(.width(32), .enable("false")) multiplexer_6 (
    .in0(bit_extender_3_out), .in1(bit_extender_4_out), .out(multiplexer_6_out), .sel(Unsigned));
  Hex_Digit_Display hex_digit_display_6 (.value(register_2_q[11:8]));  // open: dp
  Hex_Digit_Display hex_digit_display_7 (.value(register_2_q[7:4]));  // open: dp
  or or_2 (or_2_out, RegWrite, mfc0);
  Hex_Digit_Display hex_digit_display_8 (.value(register_2_q[3:0]));  // open: dp
  \ALU控制  \alu控制_1  (
    .FUNCT(if_id_1_ir_out[5:0]), .OP(if_id_1_ir_out[31:26]), .alu_op(ALUop), .pause(Syscall), .jmp(Jmp),
    .alu_source(ALUSrc), .beq(beq), .bne(bne), .RegDes(RegDst), .RegWrite(RegWrite), .MemWrite(MemWrite),
    .MemRead(MemRead), .jal(jal), .toReg(toReg), .jr(jr), .\R型指令 (\R型指令 ), .Unsigned(Unsigned),
    .shamt(Shamt), .bgez(bgez_t), .srav(srav), .lh(lh));
  Comparator #(.width(32)) comparator_2 (.a(32'ha), .b(main_1_v0_value), .eq(comparator_2_eq));  // open: gt, lt
  and and_2 (PAUSE, comparator_2_eq, Syscall);
  \ACM1401_U201414620_胡汉鹏_regfile_main  main_1 (
    .Reg1_num(if_id_1_ir_out[25:21]), .Reg2(multiplexer_3_out), .Write_Reg_num(multiplexer_5_out),
    .Din(multiplexer_18_out), .Write_Enable(or_2_out), .Clock(clk), .Reg1(main_1_reg1),
    .Reg2_2(main_1_reg2_2), .v0_Value(main_1_v0_value), .a0_Value(a0), .s2_Value(sp));  // open: ra_Value
  // Probe on multiplexer_6_out
  Multiplexer #(.width(32), .enable("false")) multiplexer_7 (
    .in0(npc), .in1(cpc), .out(multiplexer_7_out), .sel(PAUSE));
  // Probe on sp
  ID_EX id_ex_1 (
    .Shamt_in(Shamt), .Aluop_in(ALUop), .AluSrc_in(ALUSrc), .R1_in(main_1_reg1), .beq_in(beq), .bne_in(bne),
    .RegDst_in(RegDst), .RegWrite_in(RegWrite), .R2_in(main_1_reg2_2), .MemWrite_in(MemWrite),
    .MemRead_in(MemRead), .toReg_in(toReg), .lh_in(lh), .srav_in(srav), .BGEZ_in(BGEZ),
    .shamt_in_2(bit_extender_2_out), .pause_in(PAUSE), .mfc0_in(mfc0), .mtc0_in(mtc0),
    .immediate_in(multiplexer_6_out), .clk(clk), .R1_out(id_ex_1_r1_out), .RegDst_out(id_ex_1_regdst_out),
    .RegWrite_out(id_ex_1_regwrite_out), .MemWrite_out(id_ex_1_memwrite_out), .R2_out(jaReg),
    .MemRead_out(id_ex_1_memread_out), .toReg_out(id_ex_1_toreg_out), .lh_out(id_ex_1_lh_out),
    .shamt_out_2(id_ex_1_shamt_out_2), .mfc0_out(id_ex_1_mfc0_out), .mtc0_out(id_ex_1_mtc0_out),
    .immediate_out(id_ex_1_immediate_out), .PC_in(if_id_1_pc_out), .PC_out(id_ex_1_pc_out));  // open: Shamt_out, Aluop_out, AluSrc_out, beq_out, bne_out, srav_out, BGEZ_out, pause_out
  // Probe on cp0_no1[2:0]
  Button \_1号中断  (.out(\_1号中断_out ));
  Button \_2号中断  (.out(\_2号中断_out ));
  Button \_3号中断  (.out(\_3号中断_out ));
  assign bit_extender_5_out = {{27{1'b0}}, id_ex_1_r1_out[4:0]};  // Bit_Extender bit_extender_5
  ir ir_1 (
    .clock(clk), .\_1号中断 (\_1号中断_out ), .\_1号中断等待 (\ir_1__1号中断等待 ), .imw(cp0_no1[2:0]),
    .\_2号中断 (\_2号中断_out ), .\_2号中断等待 (\ir_1__2号中断等待 ), .\_3号中断 (\_3号中断_out ), .\_3号中断等待 (\ir_1__3号中断等待 ),
    .ret(eret), .ir_no(ir_1_ir_no), .rd(rd), .cp0_epc(cp0_epc), .npc(multiplexer_7_out), .cp0_R(cp0_R1),
    .mtc0(mtc0), .jaReg(jaReg), .cp0_no1(cp0_no1), .trap(trap));
  Multiplexer #(.width(32), .enable("false")) multiplexer_8 (
    .in0(id_ex_1_shamt_out_2), .in1(bit_extender_5_out), .out(multiplexer_8_out), .sel(srav));
  LED led_1 (.in(\ir_1__1号中断等待 ));
  LED led_2 (.in(\ir_1__2号中断等待 ));
  LED led_3 (.in(\ir_1__3号中断等待 ));
  // Probe on cp0_epc
  Multiplexer #(.width(32), .enable("false")) multiplexer_9 (
    .in0(id_ex_1_r1_out), .in1(jaReg), .out(multiplexer_9_out), .sel(Shamt));
  Multiplexer #(.select(2), .width(32), .enable("false")) multiplexer_10 (
    .in0(jaReg), .in1(id_ex_1_immediate_out), .in2(multiplexer_8_out), .in3(multiplexer_8_out),
    .out(multiplexer_10_out), .sel({Shamt, ALUSrc}));
  // Probe on ir_1_ir_no
  ALU alu_1 (
    .AluOP(ALUop), .X(multiplexer_9_out), .Equal(alu_1_equal), .Result(alu_1_result), .Y(multiplexer_11_out));  // open: Signed_Overflow, Result_2, UnSigned_Overflow
  Multiplexer #(.width(32), .enable("false")) multiplexer_11 (
    .in0(multiplexer_10_out), .in1({32{1'b0}}), .out(multiplexer_11_out), .sel(BGEZ));
  // Probe on total
  // Probe on Rtype
  // Probe on Itype
  // Probe on Jtype
  Shifter #(.width(32)) shifter_2 (.in(multiplexer_6_out), .\dist (5'b00010), .out(shifter_2_out));
  Adder #(.width(32)) adder_2 (.a(if_id_1_pc_out), .b(shifter_2_out), .out(adder_2_out));  // open: cin, cout
  EX_Mem ex_mem_1 (
    .PC_in(id_ex_1_pc_out), .AluResult_in(alu_1_result), .clk(clk), .RegDst_in(id_ex_1_regdst_out),
    .RegWrite_in(id_ex_1_regwrite_out), .MemWrite_in(id_ex_1_memwrite_out), .MemRead_in(id_ex_1_memread_out),
    .toReg_in(id_ex_1_toreg_out), .lh_in(id_ex_1_lh_out), .mfc0_in(id_ex_1_mfc0_out),
    .mtc0_in(id_ex_1_mtc0_out), .PC_out(ex_mem_1_pc_out), .AluResult_out(ex_mem_1_aluresult_out),
    .RegDst_out(ex_mem_1_regdst_out), .RegWrite_out(ex_mem_1_regwrite_out), .MemWrite_out(MemWrite),
    .MemRead_out(MemRead), .toReg_out(ex_mem_1_toreg_out), .lh_out(lh), .mfc0_out(ex_mem_1_mfc0_out),
    .mfc0_out_2(ex_mem_1_mfc0_out_2), .R1_in(jaReg), .R1_out(ex_mem_1_r1_out));
  Multiplexer #(.width(32), .enable("false")) multiplexer_12 (
    .in0(if_id_1_pc_out), .in1(adder_2_out), .out(multiplexer_12_out), .sel(or_3_out));
  or or_3 (or_3_out, and_3_out, and_4_out, and_5_out);
  and and_3 (and_3_out, bne, not_3_out);
  and and_4 (and_4_out, beq, alu_1_equal);
  not not_3 (not_3_out, alu_1_equal);
  and and_5 (and_5_out, ~ex_mem_1_aluresult_out[0], BGEZ);  // AND_Gate
  Multiplexer #(.select(2), .width(32), .enable("false")) multiplexer_13 (
    .in0({if_id_1_pc_out[31:28], shifter_1_out}), .in1(multiplexer_12_out), .in2(jaReg), .in3(jaReg),
    .out(multiplexer_13_out), .sel(Jmp));
  // Probe on Jmp
  Multiplexer #(.width(32), .enable("false")) multiplexer_14 (
    .in0(multiplexer_13_out), .in1(cp0_epc), .out(multiplexer_14_out), .sel(eret));
  RAM #(.addrWidth(24), .dataWidth(32), .bus("separate")) ram_1 (
    .addr(ex_mem_1_aluresult_out[25:2]), .din(ex_mem_1_r1_out), .data(ram_1_data), .str(MemWrite), .clk(clk),
    .ld(MemRead), .clr(in_1));  // open: sel
  Multiplexer #(.width(16), .enable("false")) multiplexer_15 (
    .in0(ram_1_data[15:0]), .in1(ram_1_data[31:16]), .out(multiplexer_15_out), .sel(ex_mem_1_aluresult_out[1]));
  assign bit_extender_6_out = {{16{multiplexer_15_out[15]}}, multiplexer_15_out};  // Bit_Extender bit_extender_6
  Multiplexer #(.width(32), .enable("false")) multiplexer_16 (
    .in0(ram_1_data), .in1(bit_extender_6_out), .out(multiplexer_16_out), .sel(lh));
  Mem_WB mem_wb_1 (
    .PC_in(ex_mem_1_pc_out), .AluResult_in(ex_mem_1_aluresult_out), .RegDst_in(ex_mem_1_regdst_out),
    .RegWrite_in(ex_mem_1_regwrite_out), .toReg_in(ex_mem_1_toreg_out), .mfc0_in(ex_mem_1_mfc0_out),
    .mtc0_in(ex_mem_1_mfc0_out_2), .PC_out(mem_wb_1_pc_out), .AluResult_out(mem_wb_1_aluresult_out),
    .toReg_out(toReg), .mfc0_out(mfc0), .MemData_in(multiplexer_16_out), .MemData_out(mem_wb_1_memdata_out));  // open: clk, RegDst_out, RegWrite_out, mtc0_out
  Multiplexer #(.select(2), .width(32), .enable("false")) multiplexer_17 (
    .in0(mem_wb_1_aluresult_out), .in1(mem_wb_1_memdata_out), .in2(mem_wb_1_pc_out), .in3(mem_wb_1_pc_out),
    .out(multiplexer_17_out), .sel(toReg));
  // Probe on toReg
  Multiplexer #(.width(32), .enable("false")) multiplexer_18 (
    .in0(multiplexer_17_out), .in1(cp0_R1), .out(multiplexer_18_out), .sel(mfc0));

  // Other names for the same wires on the sheet: 清零 = in_1

  // Notes on the sheet:
  //   contents of rom_1 (hex, n*v repeats v):
  //   201d0800 20110001 8000c06 20110001 20120002 20130003 8000c0a 20110001 20120002 20130003 8000c0e
  //   20110001 20120002 20130003 8000c12 20110001 20120002 20130003 c000cb9 20100001 20110001 118fc0
  //   112020 20020022 c 118882 12200001 8000c16 112020 20020022 c 20110001 118880 112020 20020022 c
  //   12200001 8000c20 20110001 118fc0 112020 20020022 c 1188c3 112020 20020022 c 118903 112020 20020022 c
  //   118903 112020 20020022 c 118903 112020 20020022 c 118903 112020 20020022 c 118903 112020 20020022 c
  //   118903 112020 20020022 c 118903 112020 20020022 c 20100001 109fc0 139fc3 8021 2012000c 24160003
  //   26100001 3210000f 20080008 20090001 139900 2709825 132020 20020022 c 1094022 1500fff9 22100001
  //   2018000f 2188024 108700 20080008 20090001 139902 2709825 132021 20020022 c 1094022 1500fff9 108702
  //   2c9b022 12c00001 8000c51 4020 1084027 84400 3508ffff 82021 20020022 c 2010ffff 20110000 ae300000
  //   22100001 22310004 ae300000 22100001 22310004 ae300000 22100001 22310004 ae300000 22100001 22310004
  //   ae300000 22100001 22310004 ae300000 22100001 22310004 ae300000 22100001 22310004 ae300000 22100001
  //   22310004 ae300000 22100001 22310004 ae300000 22100001 22310004 ae300000 22100001 22310004 ae300000
  //   22100001 22310004 ae300000 22100001 22310004 ae300000 22100001 22310004 ae300000 22100001 22310004
  //   ae300000 22100001 22310004 22100001 8020 2011003c 8e130000 8e340000 274402a 11000002 ae330000
  //   ae140000 2231fffc 1611fff8 102020 20020022 c 22100004 2011003c 1611fff2 2002000a c 20100000 22100001
  //   102020 20020022 c 22100002 102020 20020022 c 22100003 102020 20020022 c 22100004 102020 20020022 c
  //   22100005 102020 20020022 c 22100006 102020 20020022 c 22100007 102020 20020022 c 22100008 102020
  //   20020022 20020022 c 3e00008
  //   contents of rom_2 (hex, n*v repeats v):
  //   201a0007 409a0800 401a0000 23bd0004 afba0000 23bd0004 afa40000 23bd0004 afa20000 23bd0004 afb00000
  //   23bd0004 afb10000 23bd0004 afb20000 23bd0004 afb30000 23bd0004 afb60000 23bd0004 afa80000 23bd0004
  //   afa90000 23bd0004 afaa0000 201a0000 409a0800 40101000 20110001 12110004 20110002 1211002c 20110003
  //   12110054 20100001 40900800 20100001 109fc0 139fc3 8021 2012000c 24160003 24100001 3210000f 20080008
  //   20090001 139900 2709825 132020 20020022 c 1094022 1500fff9 2010000f 3210000f 108700 20080008
  //   20090001 139902 2709825 132021 20020022 c 1094022 1500fff9 2c9b022 12c00001 8000c2a 4020 1084027
  //   84400 3508ffff 82021 20020022 c 8000ca0 20100003 40900800 20100001 109fc0 139fc3 8021 2012000c
  //   24160003 24100002 3210000f 20080008 20090001 139900 2709825 132020 20020022 c 1094022 1500fff9
  //   2010000f 3210000f 108700 20080008 20090001 139902 2709825 132021 20020022 c 1094022 1500fff9 2c9b022
  //   12c00001 8000c54 4020 1084027 84400 3508ffff 82021 20020022 c 8000ca0 20100007 40900800 20100001
  //   109fc0 139fc3 8021 2012000c 24160003 24100003 3210000f 20080008 20090001 139900 2709825 132020
  //   20020022 c 1094022 1500fff9 2010000f 3210000f 108700 20080008 20090001 139902 2709825 132021
  //   20020022 c 1094022 1500fff9 2c9b022 12c00001 8000c7e 4020 1084027 84400 3508ffff 82021 20020022 c
  //   8000ca0 201a0007 409a0800 8faa0000 20010004 3a1e822 8fa90000 20010004 3a1e822 8fa80000 20010004
  //   3a1e822 8fb60000 20010004 3a1e822 8fb30000 20010004 3a1e822 8fb20000 20010004 3a1e822 8fb10000
  //   20010004 3a1e822 8fb00000 20010004 3a1e822 8fa20000 20010004 3a1e822 8fa40000 20010004 3a1e822
  //   8fba0000 20010004 3a1e822 409a0000 201a0000 409a0800 42000018
  //   rs
  //   rt
  //   rd
  //   shamt
  //   immediate
endmodule

// 控制器
module \ALU控制  (
  input  [5:0] FUNCT,
  input  [5:0] OP,
  output MemRead,
  output MemWrite,
  output [1:0] RegDes,
  output [1:0] toReg,
  output alu_source,
  output \R型指令 ,
  output RegWrite,
  output [3:0] alu_op,
  output pause,
  output [1:0] jmp,
  output jr,
  output jal,
  output bne,
  output beq,
  output bgez,
  output lh,
  output Unsigned,
  output srav,
  output shamt
);

  wire or_2_out, or_4_out, or_6_out, or_10_out, or_11_out, or_12_out, or_13_out, trans_1_i1, trans_1_i1_2,
       trans_1_i2, trans_1_i2_2, trans_1_i3_2, trans_1_i4_2, trans_1_i5_2, trans_1_i6, trans_1_i6_2,
       trans_1_i7, trans_1_i7_2, trans_1_i8, trans_1_i8_2, trans_1_i9, trans_1_i9_2, trans_1_i10_2,
       trans_1_i11_2, trans_1_i12_2, trans_1_xori;
  wire [3:0] multiplexer_1_out, multiplexer_2_out, multiplexer_3_out, multiplexer_4_out, multiplexer_5_out,
       multiplexer_6_out, multiplexer_7_out, multiplexer_8_out, multiplexer_9_out, multiplexer_11_out,
       multiplexer_12_out;

  trans trans_1 (
    .a0(FUNCT[0]), .a1(FUNCT[1]), .a2(FUNCT[2]), .a3(FUNCT[3]), .a4(FUNCT[4]), .a5(FUNCT[5]), .a6(OP[0]),
    .a7(OP[1]), .a8(OP[2]), .a9(OP[3]), .a10(OP[4]), .a11(OP[5]), .i1_2(trans_1_i1_2), .i2(trans_1_i2),
    .i3(MemWrite), .i4(beq), .i5(bne), .i6(trans_1_i6), .i7(trans_1_i7), .i8(trans_1_i8), .i9(trans_1_i9),
    .i10(jal), .i11(jmp[1]), .i12(pause), .i1(trans_1_i1), .i2_2(trans_1_i2_2), .i3_2(trans_1_i3_2),
    .i4_2(trans_1_i4_2), .i5_2(trans_1_i5_2), .i6_2(trans_1_i6_2), .i7_2(trans_1_i7_2), .i8_2(trans_1_i8_2),
    .i9_2(trans_1_i9_2), .i10_2(trans_1_i10_2), .i11_2(trans_1_i11_2), .i12_2(trans_1_i12_2), .srav(srav),
    .xori(trans_1_xori), .lh(lh), .bgez(bgez));
  or or_1 (alu_source, MemWrite, or_2_out);
  or or_2 (or_2_out, trans_1_xori, lh, trans_1_i2_2, trans_1_i3_2, trans_1_i6_2, trans_1_i12_2, trans_1_i7, trans_1_i2);
  nor nor_1 (jmp[0], jal, trans_1_i9);
  not not_1 (RegDes[0], alu_source);
  or or_3 (MemRead, lh, trans_1_i2);
  or or_4 (or_4_out, trans_1_i7, trans_1_i6);
  or or_5 (RegWrite, or_2_out, or_6_out, jal);
  or or_6 (or_6_out, trans_1_i1, trans_1_i4_2, trans_1_i5_2, trans_1_i7_2, trans_1_i8_2, trans_1_i9_2, trans_1_i11_2, trans_1_i1_2, trans_1_i6, trans_1_i8, trans_1_i10_2, srav);
  or or_7 (\R型指令 , or_6_out, jmp[1], pause);
  or or_8 (Unsigned, trans_1_xori, trans_1_i3_2, trans_1_i4_2, trans_1_i6_2, trans_1_i12_2, trans_1_i8);
  Multiplexer #(.width(4), .enable("false")) multiplexer_1 (
    .in0(multiplexer_2_out), .in1(4'b1001), .out(multiplexer_1_out), .sel(trans_1_xori));
  Multiplexer #(.width(4), .enable("false")) multiplexer_2 (
    .in0(4'b0101), .in1(4'b1011), .out(multiplexer_2_out), .sel(bgez));
  or or_9 (shamt, srav, trans_1_i7_2, trans_1_i8_2, trans_1_i9_2);
  Multiplexer #(.width(4), .enable("false")) multiplexer_3 (
    .in0(multiplexer_4_out), .in1(4'b1011), .out(multiplexer_3_out), .sel(or_4_out));
  Multiplexer #(.width(4), .enable("false")) multiplexer_4 (
    .in0(multiplexer_1_out), .in1(4'b1100), .out(multiplexer_4_out), .sel(trans_1_i8));
  or or_10 (or_10_out, trans_1_i1, trans_1_i2_2, trans_1_i3_2, trans_1_i4_2);
  or or_11 (or_11_out, trans_1_i5_2, trans_1_i6_2);
  or or_12 (or_12_out, trans_1_i11_2, trans_1_i12_2);
  Multiplexer #(.width(4), .enable("false")) multiplexer_5 (
    .in0(multiplexer_3_out), .in1(4'b1010), .out(multiplexer_5_out), .sel(trans_1_i1_2));
  or or_13 (or_13_out, srav, trans_1_i8_2);
  Multiplexer #(.width(4), .enable("false")) multiplexer_6 (
    .in0(multiplexer_5_out), .in1(4'b1000), .out(multiplexer_6_out), .sel(or_12_out));
  Multiplexer #(.width(4), .enable("false")) multiplexer_7 (
    .in0(multiplexer_8_out), .in1(4'b0001), .out(multiplexer_7_out), .sel(or_13_out));
  Multiplexer #(.width(4), .enable("false")) multiplexer_8 (
    .in0(multiplexer_9_out), .in1(4'b0010), .out(multiplexer_8_out), .sel(trans_1_i9_2));
  Multiplexer #(.width(4), .enable("false")) multiplexer_9 (
    .in0(multiplexer_6_out), .in1(4'b0110), .out(multiplexer_9_out), .sel(trans_1_i10_2));
  Multiplexer #(.width(4), .enable("false")) multiplexer_10 (
    .in0(multiplexer_11_out), .in1(4'b0101), .out(alu_op), .sel(or_10_out));
  Multiplexer #(.width(4), .enable("false")) multiplexer_11 (
    .in0(multiplexer_12_out), .in1(4'b0111), .out(multiplexer_11_out), .sel(or_11_out));
  Multiplexer #(.width(4), .enable("false")) multiplexer_12 (
    .in0(multiplexer_7_out), .in1(4'b0000), .out(multiplexer_12_out), .sel(trans_1_i7_2));

  assign jr = jmp[1];
  assign RegDes[1] = jal;
  assign toReg = {jal, MemRead};
endmodule

module trans (
  input  a0,
  input  a1,
  input  a2,
  input  a3,
  input  a4,
  input  a5,
  input  a6,
  input  a7,
  input  a8,
  input  a9,
  input  a10,
  input  a11,
  output srav,
  output i1,
  output i1_2,
  output i2,
  output xori,
  output i2_2,
  output i3,
  output lh,
  output i3_2,
  output i4,
  output bgez,
  output i5,
  output i4_2,
  output i6,
  output i5_2,
  output i7,
  output i6_2,
  output i8,
  output i7_2,
  output i9,
  output i10,
  output i8_2,
  output i11,
  output i9_2,
  output i12,
  output i10_2,
  output i11_2,
  output i12_2
);

  wire not_1_out, not_2_out, not_3_out, not_4_out, not_5_out, not_6_out, not_7_out, not_8_out, not_9_out,
       not_10_out, not_11_out, not_12_out, not_13_out, not_14_out, not_15_out, not_16_out, not_17_out,
       not_18_out, not_19_out, not_20_out, not_21_out, not_22_out, not_23_out, not_24_out, not_25_out,
       not_26_out, not_27_out, not_28_out, not_29_out, not_30_out, not_31_out, not_32_out, not_33_out,
       not_34_out, not_35_out, not_36_out, not_37_out, not_38_out, not_39_out, not_40_out, not_41_out,
       not_42_out, not_43_out, not_44_out, not_45_out, not_46_out, not_47_out, not_48_out, not_49_out,
       not_50_out, not_51_out, not_52_out, not_53_out, not_54_out, not_55_out, not_56_out, not_57_out,
       not_58_out, not_59_out, not_60_out, not_61_out, not_62_out, not_63_out, not_64_out, not_65_out,
       not_66_out, not_67_out, not_68_out, not_69_out, not_70_out, not_71_out, not_72_out, not_73_out,
       not_74_out, not_75_out, not_76_out, not_77_out, not_78_out, not_79_out, not_80_out, not_81_out,
       not_82_out, not_83_out, not_84_out, not_85_out, not_86_out, not_87_out, not_88_out, not_89_out,
       not_90_out, not_91_out, not_92_out, not_93_out, not_94_out, not_95_out, not_96_out, not_97_out,
       not_98_out, not_99_out, not_100_out, not_101_out, not_102_out, not_103_out, not_104_out, not_105_out,
       not_106_out, not_107_out, not_108_out, not_109_out, not_110_out, not_111_out, not_112_out,
       not_113_out, not_114_out, not_115_out, not_116_out, not_117_out, not_118_out, not_119_out,
       not_120_out, not_121_out, not_122_out, not_123_out, not_124_out, not_125_out, not_126_out,
       not_127_out, not_128_out, not_129_out, not_130_out, not_131_out, not_132_out, not_133_out,
       not_134_out, not_135_out, not_136_out, not_137_out, not_138_out, not_139_out, not_140_out,
       not_141_out, not_142_out, not_143_out, not_144_out, not_145_out, not_146_out, not_147_out,
       not_148_out, not_149_out, not_150_out, not_151_out, not_152_out, not_153_out, not_154_out,
       not_155_out, not_156_out, not_157_out, not_158_out, not_159_out, not_160_out, not_161_out,
       not_162_out, not_163_out, not_164_out, not_165_out, not_166_out, not_167_out, not_168_out,
       not_169_out, not_170_out, not_171_out, not_172_out, not_173_out, not_174_out, not_175_out,
       not_176_out, not_177_out, not_178_out, not_179_out, not_180_out, not_181_out, not_182_out,
       not_183_out, not_184_out, not_185_out, not_186_out, not_187_out, not_188_out, not_189_out,
       not_190_out, not_191_out, not_192_out, not_193_out;

  not not_1 (not_1_out, a11);
  not not_2 (not_2_out, a10);
  not not_3 (not_3_out, a9);
  not not_4 (not_4_out, a8);
  not not_5 (not_5_out, a7);
  not not_6 (not_6_out, a6);
  not not_7 (not_7_out, a4);
  not not_8 (not_8_out, a3);
  not not_9 (not_9_out, a2);
  not not_10 (not_10_out, a1);
  not not_11 (not_11_out, a0);
  not not_12 (not_12_out, a11);
  not not_13 (not_13_out, a10);
  not not_14 (not_14_out, a8);
  not not_15 (not_15_out, a7);
  not not_16 (not_16_out, a6);
  not not_17 (not_17_out, a11);
  not not_18 (not_18_out, a10);
  not not_19 (not_19_out, a8);
  not not_20 (not_20_out, a7);
  not not_21 (not_21_out, a11);
  not not_22 (not_22_out, a10);
  not not_23 (not_23_out, a9);
  not not_24 (not_24_out, a8);
  not not_25 (not_25_out, a7);
  not not_26 (not_26_out, a6);
  not not_27 (not_27_out, a4);
  not not_28 (not_28_out, a3);
  not not_29 (not_29_out, a2);
  not not_30 (not_30_out, a1);
  not not_31 (not_31_out, a11);
  not not_32 (not_32_out, a10);
  not not_33 (not_33_out, a9);
  not not_34 (not_34_out, a8);
  not not_35 (not_35_out, a7);
  not not_36 (not_36_out, a6);
  not not_37 (not_37_out, a4);
  not not_38 (not_38_out, a3);
  not not_39 (not_39_out, a1);
  not not_40 (not_40_out, a0);
  not not_41 (not_41_out, a11);
  not not_42 (not_42_out, a10);
  not not_43 (not_43_out, a7);
  not not_44 (not_44_out, a6);
  not not_45 (not_45_out, a11);
  not not_46 (not_46_out, a10);
  not not_47 (not_47_out, a9);
  not not_48 (not_48_out, a8);
  not not_49 (not_49_out, a7);
  not not_50 (not_50_out, a6);
  not not_51 (not_51_out, a5);
  not not_52 (not_52_out, a4);
  not not_53 (not_53_out, a3);
  not not_54 (not_54_out, a2);
  not not_55 (not_55_out, a1);
  not not_56 (not_56_out, a0);
  not not_57 (not_57_out, a11);
  not not_58 (not_58_out, a10);
  not not_59 (not_59_out, a9);
  not not_60 (not_60_out, a8);
  not not_61 (not_61_out, a7);
  not not_62 (not_62_out, a6);
  not not_63 (not_63_out, a5);
  not not_64 (not_64_out, a4);
  not not_65 (not_65_out, a3);
  not not_66 (not_66_out, a2);
  not not_67 (not_67_out, a11);
  not not_68 (not_68_out, a10);
  not not_69 (not_69_out, a9);
  not not_70 (not_70_out, a8);
  not not_71 (not_71_out, a7);
  not not_72 (not_72_out, a6);
  not not_73 (not_73_out, a5);
  not not_74 (not_74_out, a4);
  not not_75 (not_75_out, a3);
  not not_76 (not_76_out, a2);
  not not_77 (not_77_out, a0);
  not not_78 (not_78_out, a11);
  not not_79 (not_79_out, a10);
  not not_80 (not_80_out, a9);
  not not_81 (not_81_out, a8);
  not not_82 (not_82_out, a7);
  not not_83 (not_83_out, a6);
  not not_84 (not_84_out, a4);
  not not_85 (not_85_out, a3);
  not not_86 (not_86_out, a2);
  not not_87 (not_87_out, a0);
  not not_88 (not_88_out, a11);
  not not_89 (not_89_out, a10);
  not not_90 (not_90_out, a9);
  not not_91 (not_91_out, a8);
  not not_92 (not_92_out, a7);
  not not_93 (not_93_out, a6);
  not not_94 (not_94_out, a4);
  not not_95 (not_95_out, a3);
  not not_96 (not_96_out, a1);
  not not_97 (not_97_out, a11);
  not not_98 (not_98_out, a10);
  not not_99 (not_99_out, a7);
  and and_1 (i1, not_1_out, not_2_out, not_3_out, not_4_out, not_5_out, not_6_out, a5, not_7_out, not_8_out, not_9_out, not_10_out, not_11_out);
  and and_2 (i2_2, not_12_out, not_13_out, a9, not_14_out, not_15_out, not_16_out);
  and and_3 (i3_2, not_17_out, not_18_out, a9, not_19_out, not_20_out, a6);
  and and_4 (i4_2, not_21_out, not_22_out, not_23_out, not_24_out, not_25_out, not_26_out, a5, not_27_out, not_28_out, not_29_out, not_30_out, a0);
  and and_5 (i5_2, not_31_out, not_32_out, not_33_out, not_34_out, not_35_out, not_36_out, a5, not_37_out, not_38_out, a2, not_39_out, not_40_out);
  and and_6 (i6_2, not_41_out, not_42_out, a9, a8, not_43_out, not_44_out);
  and and_7 (i7_2, not_45_out, not_46_out, not_47_out, not_48_out, not_49_out, not_50_out, not_51_out, not_52_out, not_53_out, not_54_out, not_55_out, not_56_out);
  and and_8 (i8_2, not_57_out, not_58_out, not_59_out, not_60_out, not_61_out, not_62_out, not_63_out, not_64_out, not_65_out, not_66_out, a1, a0);
  and and_9 (i9_2, not_67_out, not_68_out, not_69_out, not_70_out, not_71_out, not_72_out, not_73_out, not_74_out, not_75_out, not_76_out, a1, not_77_out);
  and and_10 (i10_2, not_78_out, not_79_out, not_80_out, not_81_out, not_82_out, not_83_out, a5, not_84_out, not_85_out, not_86_out, a1, not_87_out);
  and and_11 (i11_2, not_88_out, not_89_out, not_90_out, not_91_out, not_92_out, not_93_out, a5, not_94_out, not_95_out, a2, not_96_out, a0);
  and and_12 (i12_2, not_97_out, not_98_out, a9, a8, not_99_out, a6);
  not not_100 (not_100_out, a11);
  not not_101 (not_101_out, a10);
  not not_102 (not_102_out, a9);
  not not_103 (not_103_out, a8);
  not not_104 (not_104_out, a7);
  not not_105 (not_105_out, a6);
  not not_106 (not_106_out, a4);
  not not_107 (not_107_out, a3);
  not not_108 (not_108_out, a10);
  not not_109 (not_109_out, a9);
  not not_110 (not_110_out, a8);
  not not_111 (not_111_out, a10);
  not not_112 (not_112_out, a8);
  not not_113 (not_113_out, a11);
  not not_114 (not_114_out, a10);
  not not_115 (not_115_out, a9);
  not not_116 (not_116_out, a7);
  not not_117 (not_117_out, a6);
  not not_118 (not_118_out, a11);
  not not_119 (not_119_out, a10);
  not not_120 (not_120_out, a9);
  not not_121 (not_121_out, a7);
  not not_122 (not_122_out, a11);
  not not_123 (not_123_out, a10);
  not not_124 (not_124_out, a9);
  not not_125 (not_125_out, a8);
  not not_126 (not_126_out, a7);
  not not_127 (not_127_out, a6);
  not not_128 (not_128_out, a4);
  not not_129 (not_129_out, a2);
  not not_130 (not_130_out, a0);
  not not_131 (not_131_out, a11);
  not not_132 (not_132_out, a10);
  not not_133 (not_133_out, a8);
  not not_134 (not_134_out, a6);
  not not_135 (not_135_out, a11);
  not not_136 (not_136_out, a10);
  not not_137 (not_137_out, a9);
  not not_138 (not_138_out, a8);
  not not_139 (not_139_out, a7);
  not not_140 (not_140_out, a6);
  not not_141 (not_141_out, a4);
  not not_142 (not_142_out, a2);
  not not_143 (not_143_out, a11);
  not not_144 (not_144_out, a10);
  not not_145 (not_145_out, a9);
  not not_146 (not_146_out, a8);
  not not_147 (not_147_out, a6);
  not not_148 (not_148_out, a11);
  not not_149 (not_149_out, a10);
  not not_150 (not_150_out, a9);
  not not_151 (not_151_out, a8);
  not not_152 (not_152_out, a11);
  not not_153 (not_153_out, a10);
  not not_154 (not_154_out, a9);
  not not_155 (not_155_out, a8);
  not not_156 (not_156_out, a7);
  not not_157 (not_157_out, a6);
  not not_158 (not_158_out, a5);
  not not_159 (not_159_out, a4);
  not not_160 (not_160_out, a2);
  not not_161 (not_161_out, a1);
  not not_162 (not_162_out, a0);
  not not_163 (not_163_out, a11);
  not not_164 (not_164_out, a10);
  not not_165 (not_165_out, a9);
  not not_166 (not_166_out, a8);
  not not_167 (not_167_out, a7);
  not not_168 (not_168_out, a6);
  not not_169 (not_169_out, a5);
  not not_170 (not_170_out, a4);
  not not_171 (not_171_out, a1);
  not not_172 (not_172_out, a0);
  and and_13 (i1_2, not_100_out, not_101_out, not_102_out, not_103_out, not_104_out, not_105_out, a5, not_106_out, not_107_out, a2, a1, a0);
  and and_14 (i2, a11, not_108_out, not_109_out, not_110_out, a7, a6);
  and and_15 (i3, a11, not_111_out, a9, not_112_out, a7, a6);
  and and_16 (i4, not_113_out, not_114_out, not_115_out, a8, not_116_out, not_117_out);
  and and_17 (i5, not_118_out, not_119_out, not_120_out, a8, not_121_out, a6);
  and and_18 (i6, not_122_out, not_123_out, not_124_out, not_125_out, not_126_out, not_127_out, a5, not_128_out, a3, not_129_out, a1, not_130_out);
  and and_19 (i7, not_131_out, not_132_out, a9, not_133_out, a7, not_134_out);
  and and_20 (i8, not_135_out, not_136_out, not_137_out, not_138_out, not_139_out, not_140_out, a5, not_141_out, a3, not_142_out, a1, a0);
  and and_21 (i9, not_143_out, not_144_out, not_145_out, not_146_out, a7, not_147_out);
  and and_22 (i10, not_148_out, not_149_out, not_150_out, not_151_out, a7, a6);
  and and_23 (i11, not_152_out, not_153_out, not_154_out, not_155_out, not_156_out, not_157_out, not_158_out, not_159_out, a3, not_160_out, not_161_out, not_162_out);
  and and_24 (i12, not_163_out, not_164_out, not_165_out, not_166_out, not_167_out, not_168_out, not_169_out, not_170_out, a3, a2, not_171_out, not_172_out);
  not not_173 (not_173_out, a3);
  not not_174 (not_174_out, a4);
  not not_175 (not_175_out, a5);
  not not_176 (not_176_out, a6);
  not not_177 (not_177_out, a7);
  not not_178 (not_178_out, a8);
  not not_179 (not_179_out, a9);
  not not_180 (not_180_out, a10);
  not not_181 (not_181_out, a11);
  not not_182 (not_182_out, a6);
  not not_183 (not_183_out, a10);
  not not_184 (not_184_out, a11);
  not not_185 (not_185_out, a7);
  not not_186 (not_186_out, a8);
  not not_187 (not_187_out, a9);
  not not_188 (not_188_out, a10);
  not not_189 (not_189_out, a7);
  not not_190 (not_190_out, a8);
  not not_191 (not_191_out, a9);
  not not_192 (not_192_out, a10);
  not not_193 (not_193_out, a11);
  and and_25 (srav, a0, a1, a2, not_173_out, not_174_out, not_175_out, not_176_out, not_177_out, not_178_out, not_179_out, not_180_out, not_181_out);
  and and_26 (xori, not_182_out, a7, a8, a9, not_183_out, not_184_out);
  and and_27 (lh, a6, not_185_out, not_186_out, not_187_out, not_188_out, a11);
  and and_28 (bgez, a6, not_189_out, not_190_out, not_191_out, not_192_out, not_193_out);
endmodule

module trans1 (
  input  a0,
  input  a1,
  input  a2,
  input  a3,
  input  a4,
  input  a5,
  input  a6,
  input  a7,
  input  a8,
  input  a9,
  input  a10,
  input  a11,
  output i1,
  output i2,
  output i3,
  output i4,
  output i5,
  output i6,
  output i7,
  output i8,
  output i9,
  output i10,
  output i11,
  output i12
);

  wire not_1_out, not_2_out, not_3_out, not_4_out, not_5_out, not_6_out, not_7_out, not_8_out, not_9_out,
       not_10_out, not_11_out, not_12_out, not_13_out, not_14_out, not_15_out, not_16_out, not_17_out,
       not_18_out, not_19_out, not_20_out, not_21_out, not_22_out, not_23_out, not_24_out, not_25_out,
       not_26_out, not_27_out, not_28_out, not_29_out, not_30_out, not_31_out, not_32_out, not_33_out,
       not_34_out, not_35_out, not_36_out, not_37_out, not_38_out, not_39_out, not_40_out, not_41_out,
       not_42_out, not_43_out, not_44_out, not_45_out, not_46_out, not_47_out, not_48_out, not_49_out,
       not_50_out, not_51_out, not_52_out, not_53_out, not_54_out, not_55_out, not_56_out, not_57_out,
       not_58_out, not_59_out, not_60_out, not_61_out, not_62_out, not_63_out, not_64_out, not_65_out,
       not_66_out, not_67_out, not_68_out, not_69_out, not_70_out, not_71_out, not_72_out, not_73_out,
       not_74_out, not_75_out, not_76_out, not_77_out, not_78_out, not_79_out, not_80_out, not_81_out,
       not_82_out, not_83_out, not_84_out, not_85_out, not_86_out, not_87_out, not_88_out, not_89_out,
       not_90_out, not_91_out, not_92_out, not_93_out, not_94_out, not_95_out, not_96_out, not_97_out,
       not_98_out, not_99_out;

  not not_1 (not_1_out, a11);
  not not_2 (not_2_out, a10);
  not not_3 (not_3_out, a9);
  not not_4 (not_4_out, a8);
  not not_5 (not_5_out, a7);
  not not_6 (not_6_out, a6);
  not not_7 (not_7_out, a4);
  not not_8 (not_8_out, a3);
  not not_9 (not_9_out, a2);
  not not_10 (not_10_out, a1);
  not not_11 (not_11_out, a0);
  not not_12 (not_12_out, a11);
  not not_13 (not_13_out, a10);
  not not_14 (not_14_out, a8);
  not not_15 (not_15_out, a7);
  not not_16 (not_16_out, a6);
  not not_17 (not_17_out, a11);
  not not_18 (not_18_out, a10);
  not not_19 (not_19_out, a8);
  not not_20 (not_20_out, a7);
  not not_21 (not_21_out, a11);
  not not_22 (not_22_out, a10);
  not not_23 (not_23_out, a9);
  not not_24 (not_24_out, a8);
  not not_25 (not_25_out, a7);
  not not_26 (not_26_out, a6);
  not not_27 (not_27_out, a4);
  not not_28 (not_28_out, a3);
  not not_29 (not_29_out, a2);
  not not_30 (not_30_out, a1);
  not not_31 (not_31_out, a11);
  not not_32 (not_32_out, a10);
  not not_33 (not_33_out, a9);
  not not_34 (not_34_out, a8);
  not not_35 (not_35_out, a7);
  not not_36 (not_36_out, a6);
  not not_37 (not_37_out, a4);
  not not_38 (not_38_out, a3);
  not not_39 (not_39_out, a1);
  not not_40 (not_40_out, a0);
  not not_41 (not_41_out, a11);
  not not_42 (not_42_out, a10);
  not not_43 (not_43_out, a7);
  not not_44 (not_44_out, a6);
  not not_45 (not_45_out, a11);
  not not_46 (not_46_out, a10);
  not not_47 (not_47_out, a9);
  not not_48 (not_48_out, a8);
  not not_49 (not_49_out, a7);
  not not_50 (not_50_out, a6);
  not not_51 (not_51_out, a5);
  not not_52 (not_52_out, a4);
  not not_53 (not_53_out, a3);
  not not_54 (not_54_out, a2);
  not not_55 (not_55_out, a1);
  not not_56 (not_56_out, a0);
  not not_57 (not_57_out, a11);
  not not_58 (not_58_out, a10);
  not not_59 (not_59_out, a9);
  not not_60 (not_60_out, a8);
  not not_61 (not_61_out, a7);
  not not_62 (not_62_out, a6);
  not not_63 (not_63_out, a5);
  not not_64 (not_64_out, a4);
  not not_65 (not_65_out, a3);
  not not_66 (not_66_out, a2);
  not not_67 (not_67_out, a11);
  not not_68 (not_68_out, a10);
  not not_69 (not_69_out, a9);
  not not_70 (not_70_out, a8);
  not not_71 (not_71_out, a7);
  not not_72 (not_72_out, a6);
  not not_73 (not_73_out, a5);
  not not_74 (not_74_out, a4);
  not not_75 (not_75_out, a3);
  not not_76 (not_76_out, a2);
  not not_77 (not_77_out, a0);
  not not_78 (not_78_out, a11);
  not not_79 (not_79_out, a10);
  not not_80 (not_80_out, a9);
  not not_81 (not_81_out, a8);
  not not_82 (not_82_out, a7);
  not not_83 (not_83_out, a6);
  not not_84 (not_84_out, a4);
  not not_85 (not_85_out, a3);
  not not_86 (not_86_out, a2);
  not not_87 (not_87_out, a0);
  not not_88 (not_88_out, a11);
  not not_89 (not_89_out, a10);
  not not_90 (not_90_out, a9);
  not not_91 (not_91_out, a8);
  not not_92 (not_92_out, a7);
  not not_93 (not_93_out, a6);
  not not_94 (not_94_out, a4);
  not not_95 (not_95_out, a3);
  not not_96 (not_96_out, a1);
  not not_97 (not_97_out, a11);
  not not_98 (not_98_out, a10);
  not not_99 (not_99_out, a7);
  and and_1 (i1, not_1_out, not_2_out, not_3_out, not_4_out, not_5_out, not_6_out, a5, not_7_out, not_8_out, not_9_out, not_10_out, not_11_out);
  and and_2 (i2, not_12_out, not_13_out, a9, not_14_out, not_15_out, not_16_out);
  and and_3 (i3, not_17_out, not_18_out, a9, not_19_out, not_20_out, a6);
  and and_4 (i4, not_21_out, not_22_out, not_23_out, not_24_out, not_25_out, not_26_out, a5, not_27_out, not_28_out, not_29_out, not_30_out, a0);
  and and_5 (i5, not_31_out, not_32_out, not_33_out, not_34_out, not_35_out, not_36_out, a5, not_37_out, not_38_out, a2, not_39_out, not_40_out);
  and and_6 (i6, not_41_out, not_42_out, a9, a8, not_43_out, not_44_out);
  and and_7 (i7, not_45_out, not_46_out, not_47_out, not_48_out, not_49_out, not_50_out, not_51_out, not_52_out, not_53_out, not_54_out, not_55_out, not_56_out);
  and and_8 (i8, not_57_out, not_58_out, not_59_out, not_60_out, not_61_out, not_62_out, not_63_out, not_64_out, not_65_out, not_66_out, a1, a0);
  and and_9 (i9, not_67_out, not_68_out, not_69_out, not_70_out, not_71_out, not_72_out, not_73_out, not_74_out, not_75_out, not_76_out, a1, not_77_out);
  and and_10 (i10, not_78_out, not_79_out, not_80_out, not_81_out, not_82_out, not_83_out, a5, not_84_out, not_85_out, not_86_out, a1, not_87_out);
  and and_11 (i11, not_88_out, not_89_out, not_90_out, not_91_out, not_92_out, not_93_out, a5, not_94_out, not_95_out, a2, not_96_out, a0);
  and and_12 (i12, not_97_out, not_98_out, a9, a8, not_99_out, a6);
endmodule

module trans2 (
  output i1,
  output i2,
  output i3,
  output i4,
  output i5,
  output i6,
  output i7,
  output i8,
  output i9,
  output i10,
  output i11,
  output i12
);

  wire a0, a1, a2, a3, a4, a5, a6, a7, a8, a9, a10, a11, not_1_out, not_2_out, not_3_out, not_4_out,
       not_5_out, not_6_out, not_7_out, not_8_out, not_9_out, not_10_out, not_11_out, not_12_out, not_13_out,
       not_14_out, not_15_out, not_16_out, not_17_out, not_18_out, not_19_out, not_20_out, not_21_out,
       not_22_out, not_23_out, not_24_out, not_25_out, not_26_out, not_27_out, not_28_out, not_29_out,
       not_30_out, not_31_out, not_32_out, not_33_out, not_34_out, not_35_out, not_36_out, not_37_out,
       not_38_out, not_39_out, not_40_out, not_41_out, not_42_out, not_43_out, not_44_out, not_45_out,
       not_46_out, not_47_out, not_48_out, not_49_out, not_50_out, not_51_out, not_52_out, not_53_out,
       not_54_out, not_55_out, not_56_out, not_57_out, not_58_out, not_59_out, not_60_out, not_61_out,
       not_62_out, not_63_out, not_64_out, not_65_out, not_66_out, not_67_out, not_68_out, not_69_out,
       not_70_out, not_71_out, not_72_out, not_73_out;

  not not_1 (not_1_out, a11);
  not not_2 (not_2_out, a10);
  not not_3 (not_3_out, a9);
  not not_4 (not_4_out, a8);
  not not_5 (not_5_out, a7);
  not not_6 (not_6_out, a6);
  not not_7 (not_7_out, a4);
  not not_8 (not_8_out, a3);
  not not_9 (not_9_out, a10);
  not not_10 (not_10_out, a9);
  not not_11 (not_11_out, a8);
  not not_12 (not_12_out, a10);
  not not_13 (not_13_out, a8);
  not not_14 (not_14_out, a11);
  not not_15 (not_15_out, a10);
  not not_16 (not_16_out, a9);
  not not_17 (not_17_out, a7);
  not not_18 (not_18_out, a6);
  not not_19 (not_19_out, a11);
  not not_20 (not_20_out, a10);
  not not_21 (not_21_out, a9);
  not not_22 (not_22_out, a7);
  not not_23 (not_23_out, a11);
  not not_24 (not_24_out, a10);
  not not_25 (not_25_out, a9);
  not not_26 (not_26_out, a8);
  not not_27 (not_27_out, a7);
  not not_28 (not_28_out, a6);
  not not_29 (not_29_out, a4);
  not not_30 (not_30_out, a2);
  not not_31 (not_31_out, a0);
  not not_32 (not_32_out, a11);
  not not_33 (not_33_out, a10);
  not not_34 (not_34_out, a8);
  not not_35 (not_35_out, a6);
  not not_36 (not_36_out, a11);
  not not_37 (not_37_out, a10);
  not not_38 (not_38_out, a9);
  not not_39 (not_39_out, a8);
  not not_40 (not_40_out, a7);
  not not_41 (not_41_out, a6);
  not not_42 (not_42_out, a4);
  not not_43 (not_43_out, a2);
  not not_44 (not_44_out, a11);
  not not_45 (not_45_out, a10);
  not not_46 (not_46_out, a9);
  not not_47 (not_47_out, a8);
  not not_48 (not_48_out, a6);
  not not_49 (not_49_out, a11);
  not not_50 (not_50_out, a10);
  not not_51 (not_51_out, a9);
  not not_52 (not_52_out, a8);
  not not_53 (not_53_out, a11);
  not not_54 (not_54_out, a10);
  not not_55 (not_55_out, a9);
  not not_56 (not_56_out, a8);
  not not_57 (not_57_out, a7);
  not not_58 (not_58_out, a6);
  not not_59 (not_59_out, a5);
  not not_60 (not_60_out, a4);
  not not_61 (not_61_out, a2);
  not not_62 (not_62_out, a1);
  not not_63 (not_63_out, a0);
  not not_64 (not_64_out, a11);
  not not_65 (not_65_out, a10);
  not not_66 (not_66_out, a9);
  not not_67 (not_67_out, a8);
  not not_68 (not_68_out, a7);
  not not_69 (not_69_out, a6);
  not not_70 (not_70_out, a5);
  not not_71 (not_71_out, a4);
  not not_72 (not_72_out, a1);
  not not_73 (not_73_out, a0);
  and and_1 (i2, a11, not_9_out, not_10_out, not_11_out, a7, a6);
  and and_2 (i3, a11, not_12_out, a9, not_13_out, a7, a6);
  and and_3 (i4, not_14_out, not_15_out, not_16_out, a8, not_17_out, not_18_out);
  and and_4 (i5, not_19_out, not_20_out, not_21_out, a8, not_22_out, a6);
  and and_5 (i7, not_32_out, not_33_out, a9, not_34_out, a7, not_35_out);
  and and_6 (i9, not_44_out, not_45_out, not_46_out, not_47_out, a7, not_48_out);
  and and_7 (i10, not_49_out, not_50_out, not_51_out, not_52_out, a7, a6);
  and and_8 (i1, not_1_out, not_2_out, not_3_out, not_4_out, not_5_out, not_6_out, a5, not_7_out, not_8_out, a2, a1, a0);
  and and_9 (i6, not_23_out, not_24_out, not_25_out, not_26_out, not_27_out, not_28_out, a5, not_29_out, a3, not_30_out, a1, not_31_out);
  and and_10 (i8, not_36_out, not_37_out, not_38_out, not_39_out, not_40_out, not_41_out, a5, not_42_out, a3, not_43_out, a1, a0);
  and and_11 (i11, not_53_out, not_54_out, not_55_out, not_56_out, not_57_out, not_58_out, not_59_out, not_60_out, a3, not_61_out, not_62_out, not_63_out);
  and and_12 (i12, not_64_out, not_65_out, not_66_out, not_67_out, not_68_out, not_69_out, not_70_out, not_71_out, a3, a2, not_72_out, not_73_out);
endmodule

module trans3 (
  input  a0,
  input  a1,
  input  a2,
  input  a3,
  input  a4,
  input  a5,
  input  a6,
  input  a7,
  input  a8,
  input  a9,
  input  a10,
  input  a11,
  output srav,
  output xori,
  output lh,
  output bgez
);

  wire not_1_out, not_2_out, not_3_out, not_4_out, not_5_out, not_6_out, not_7_out, not_8_out, not_9_out,
       not_10_out, not_11_out, not_12_out, not_13_out, not_14_out, not_15_out, not_16_out, not_17_out,
       not_18_out, not_19_out, not_20_out, not_21_out;

  not not_1 (not_1_out, a3);
  not not_2 (not_2_out, a4);
  not not_3 (not_3_out, a5);
  not not_4 (not_4_out, a6);
  not not_5 (not_5_out, a7);
  not not_6 (not_6_out, a8);
  not not_7 (not_7_out, a9);
  not not_8 (not_8_out, a10);
  not not_9 (not_9_out, a11);
  not not_10 (not_10_out, a6);
  not not_11 (not_11_out, a10);
  not not_12 (not_12_out, a11);
  not not_13 (not_13_out, a7);
  not not_14 (not_14_out, a8);
  not not_15 (not_15_out, a9);
  not not_16 (not_16_out, a10);
  not not_17 (not_17_out, a7);
  not not_18 (not_18_out, a8);
  not not_19 (not_19_out, a9);
  not not_20 (not_20_out, a10);
  not not_21 (not_21_out, a11);
  and and_1 (srav, a0, a1, a2, not_1_out, not_2_out, not_3_out, not_4_out, not_5_out, not_6_out, not_7_out, not_8_out, not_9_out);
  and and_2 (xori, not_10_out, a7, a8, a9, not_11_out, not_12_out);
  and and_3 (lh, a6, not_13_out, not_14_out, not_15_out, not_16_out, a11);
  and and_4 (bgez, a6, not_17_out, not_18_out, not_19_out, not_20_out, not_21_out);
endmodule

module ir (
  input  clock,
  input  \_1号中断 ,
  input  [2:0] imw,
  input  \_2号中断 ,
  input  \_3号中断 ,
  input  ret,
  input  [31:0] npc,
  input  [31:0] jaReg,
  input  mtc0,
  input  [4:0] rd,
  output \_1号中断等待 ,
  output \_2号中断等待 ,
  output [1:0] ir_no,
  output \_3号中断等待 ,
  output trap,
  output [31:0] cp0_epc,
  output [31:0] cp0_R,
  output [31:0] cp0_no1
);

  wire and_1_out, and_2_out, and_3_out, and_4_out, and_5_out, and_6_out, clock_1_out, d_ff_1_q, d_ff_2_q,
       d_ff_3_q, d_ff_4_q, d_ff_5_q, d_ff_6_q, demultiplexer_1_out1, demultiplexer_1_out2,
       demultiplexer_1_out3, demultiplexer_2_out0, demultiplexer_2_out1, ir_q, or_4_out, or_5_out, or_6_out,
       or_7_out, priority_encoder_1_gs;
  wire [1:0] multiplexer_3_out, priority_encoder_1_out;
  wire [31:0] bit_extender_1_out, multiplexer_1_out;
  wire [31:2] reset;

  Clock clock_1 (.out(clock_1_out));
  Demultiplexer #(.select(2), .enable("false")) demultiplexer_1 (
    .out1(demultiplexer_1_out1), .out2(demultiplexer_1_out2), .out3(demultiplexer_1_out3), .in(1'b1),
    .sel(ir_no));  // open: out0
  Demultiplexer #(.select(2), .enable("false")) demultiplexer_2 (
    .out0(demultiplexer_2_out0), .out1(demultiplexer_2_out1), .in(mtc0), .sel(rd[1:0]));  // open: out2, out3
  Multiplexer #(.width(32), .enable("false")) multiplexer_1 (
    .in0(npc), .in1(jaReg), .out(multiplexer_1_out), .sel(mtc0));
  or or_1 (\_1号中断等待 , d_ff_1_q, d_ff_4_q);
  or or_2 (\_2号中断等待 , d_ff_2_q, d_ff_5_q);
  or or_3 (\_3号中断等待 , d_ff_3_q, d_ff_6_q);
  or or_4 (or_4_out, demultiplexer_2_out0, trap);
  D_Flip_Flop d_ff_1 (.clk(\_1号中断 ), .D(1'b1), .Q(d_ff_1_q), .reset(d_ff_4_q));  // open: Qn, preset, en
  D_Flip_Flop d_ff_2 (.clk(\_2号中断 ), .D(1'b1), .Q(d_ff_2_q), .reset(d_ff_5_q));  // open: Qn, preset, en
  D_Flip_Flop d_ff_3 (.clk(\_3号中断 ), .D(1'b1), .Q(d_ff_3_q), .reset(d_ff_6_q));  // open: Qn, preset, en
  Register #(.width(32)) u_cp0_no1 (.D(jaReg), .en(demultiplexer_2_out1), .Q(cp0_no1), .clk(clock));  // open: clr
  or or_5 (or_5_out, d_ff_1_q, d_ff_4_q);
  or or_6 (or_6_out, d_ff_2_q, d_ff_5_q);
  or or_7 (or_7_out, d_ff_3_q, d_ff_6_q);
  Register #(.width(32)) cp0_no0 (.D(multiplexer_1_out), .en(or_4_out), .Q(cp0_epc), .clk(clock));  // open: clr
  and and_1 (and_1_out, or_5_out, ~demultiplexer_1_out1);  // AND_Gate
  and and_2 (and_2_out, or_6_out, ~demultiplexer_1_out2);  // AND_Gate
  and and_3 (and_3_out, or_7_out, ~demultiplexer_1_out3);  // AND_Gate
  Multiplexer #(.select(2), .width(32), .enable("false")) multiplexer_2 (
    .in0(cp0_epc), .in1(cp0_no1), .in2({reset, ir_no}), .out(cp0_R), .sel(rd[1:0]));  // open: in3
  D_Flip_Flop d_ff_4 (.clk(clock), .D(and_1_out), .Q(d_ff_4_q));  // open: Qn, preset, en, reset
  D_Flip_Flop d_ff_5 (.clk(clock), .D(and_2_out), .Q(d_ff_5_q));  // open: Qn, preset, en, reset
  D_Flip_Flop d_ff_6 (.clk(clock), .D(and_3_out), .Q(d_ff_6_q));  // open: Qn, preset, en, reset
  and and_4 (and_4_out, d_ff_4_q, ~imw[0]);  // AND_Gate
  and and_5 (and_5_out, d_ff_5_q, ~imw[1]);  // AND_Gate
  and and_6 (and_6_out, d_ff_6_q, ~imw[2]);  // AND_Gate
  Priority_Encoder #(.select(2)) priority_encoder_1 (
    .in0(1'b0), .in1(and_4_out), .in2(and_5_out), .in3(and_6_out), .out(priority_encoder_1_out),
    .gs(priority_encoder_1_gs), .en_in(1'b1));  // open: en_out
  // Probe on multiplexer_3_out
  Multiplexer #(.width(2), .enable("false")) multiplexer_3 (
    .in0(2'b00), .in1(priority_encoder_1_out), .out(multiplexer_3_out), .sel(priority_encoder_1_gs));
  Register #(.width(1)) ir (.D(priority_encoder_1_gs), .Q(ir_q), .clk(clock));  // open: en, clr
  assign bit_extender_1_out = {{30{1'b0}}, multiplexer_3_out};  // Bit_Extender bit_extender_1
  and and_7 (trap, ir_q, priority_encoder_1_gs);
  Register #(.width(32)) cp0_no2 (
    .D(bit_extender_1_out), .en(priority_encoder_1_gs), .Q({reset, ir_no}), .clk(clock));  // open: clr

  // Other names for the same wires on the sheet: reset[1:0] = ir_no
endmodule

module cpo_instru (
  input  [31:0] in_1,
  output out_2,
  output out_3,
  output out_4
);

  wire and_1_out, and_2_out, and_3_out, and_4_out, and_5_out;

  and and_1 (and_1_out, ~in_1[0], ~in_1[1], ~in_1[2], in_1[3], in_1[4], ~in_1[5]);  // AND_Gate
  and and_2 (and_2_out, ~in_1[26], ~in_1[27], ~in_1[28], ~in_1[29], in_1[30], ~in_1[31]);  // AND_Gate
  and and_3 (and_3_out, ~in_1[21], ~in_1[22], ~in_1[23], ~in_1[24], in_1[25]);  // AND_Gate
  and and_4 (and_4_out, ~in_1[21], ~in_1[22], ~in_1[23], ~in_1[24], ~in_1[25]);  // AND_Gate
  and and_5 (and_5_out, ~in_1[21], ~in_1[22], in_1[23], ~in_1[24], ~in_1[25]);  // AND_Gate
  and and_6 (out_2, and_1_out, and_3_out, and_2_out);
  and and_7 (out_3, and_2_out, and_4_out);
  and and_8 (out_4, and_2_out, and_5_out);

  // Notes on the sheet:
  //   op
endmodule

module ir_test (
  input  [2:0] IMW,
  input  in_2
);

  wire \_1号中断_out , \_2号中断_out , \_3号中断_out , and_1_out, and_2_out, and_3_out, and_4_out, and_5_out,
       and_6_out, clk, clock, comparator_1_lt, comparator_2_gt, d_ff_1_q, d_ff_2_q, d_ff_3_q, d_ff_4_q,
       d_ff_5_q, d_ff_6_q, demultiplexer_1_out1, demultiplexer_1_out2, demultiplexer_1_out3, mtc0,
       multiplexer_3_out, multiplexer_4_out, or_1_out, or_2_out, or_3_out, or_4_out, or_5_out, or_6_out,
       priority_encoder_1_gs, trap;
  wire [1:0] ir_no, multiplexer_2_out, priority_encoder_1_out, reset;
  wire [4:0] rd;
  wire [31:0] bit_extender_1_out, cp0_epc, cp0_no1, cp0_no2, cp0_R1, jaReg, npc;

  Clock clock_1 (.out(clock));
  Button \_1号中断  (.out(\_1号中断_out ));
  LED led_1 (.in(or_1_out));
  Button \_2号中断  (.out(\_2号中断_out ));
  LED led_2 (.in(or_2_out));
  Demultiplexer #(.select(2), .enable("false")) demultiplexer_1 (
    .out1(demultiplexer_1_out1), .out2(demultiplexer_1_out2), .out3(demultiplexer_1_out3), .in(1'b1),
    .sel(reset));  // open: out0
  Button \_3号中断  (.out(\_3号中断_out ));
  LED led_3 (.in(or_3_out));
  assign bit_extender_1_out = {{30{1'b0}}, ir_no};  // Bit_Extender bit_extender_1
  // Probe on cp0_epc
  Register #(.width(32)) cp0_no0 (.D(npc), .Q(cp0_epc), .clk(trap));  // open: en, clr
  Register #(.width(32)) u_cp0_no1 (.D(jaReg), .en(mtc0), .Q(cp0_no1), .clk(clk));  // open: clr
  Register #(.width(32)) u_cp0_no2 (.D(bit_extender_1_out), .Q(cp0_no2), .clk(trap));  // open: en, clr
  or or_1 (or_1_out, d_ff_1_q, d_ff_4_q);
  or or_2 (or_2_out, d_ff_2_q, d_ff_5_q);
  or or_3 (or_3_out, d_ff_3_q, d_ff_6_q);
  Multiplexer #(.select(2), .width(32), .enable("false")) multiplexer_1 (
    .in0(cp0_epc), .in1(cp0_no1), .in2(cp0_no2), .out(cp0_R1), .sel(rd[1:0]));  // open: in3
  // Probe on rd
  // Probe on cp0_no2
  D_Flip_Flop d_ff_1 (.clk(\_1号中断_out ), .D(1'b1), .Q(d_ff_1_q), .reset(d_ff_4_q));  // open: Qn, preset, en
  D_Flip_Flop d_ff_2 (.clk(\_2号中断_out ), .D(1'b1), .Q(d_ff_2_q), .reset(d_ff_5_q));  // open: Qn, preset, en
  D_Flip_Flop d_ff_3 (.clk(\_3号中断_out ), .D(1'b1), .Q(d_ff_3_q), .reset(d_ff_6_q));  // open: Qn, preset, en
  // Probe on cp0_R1
  or or_4 (or_4_out, d_ff_1_q, d_ff_4_q);
  or or_5 (or_5_out, d_ff_2_q, d_ff_5_q);
  or or_6 (or_6_out, d_ff_3_q, d_ff_6_q);
  and and_1 (and_1_out, or_4_out, ~demultiplexer_1_out1);  // AND_Gate
  and and_2 (and_2_out, or_5_out, ~demultiplexer_1_out2);  // AND_Gate
  and and_3 (and_3_out, or_6_out, ~demultiplexer_1_out3);  // AND_Gate
  D_Flip_Flop d_ff_4 (.clk(clock), .D(and_1_out), .Q(d_ff_4_q));  // open: Qn, preset, en, reset
  D_Flip_Flop d_ff_5 (.clk(clock), .D(and_2_out), .Q(d_ff_5_q));  // open: Qn, preset, en, reset
  D_Flip_Flop d_ff_6 (.clk(clock), .D(and_3_out), .Q(d_ff_6_q));  // open: Qn, preset, en, reset
  and and_4 (and_4_out, d_ff_4_q, ~IMW[0]);  // AND_Gate
  and and_5 (and_5_out, d_ff_5_q, ~IMW[1]);  // AND_Gate
  and and_6 (and_6_out, d_ff_6_q, ~IMW[2]);  // AND_Gate
  Priority_Encoder #(.select(2)) priority_encoder_1 (
    .in0(1'b0), .in1(and_4_out), .in2(and_5_out), .in3(and_6_out), .out(priority_encoder_1_out),
    .gs(priority_encoder_1_gs), .en_in(1'b1));  // open: en_out
  // Probe on multiplexer_2_out
  Multiplexer #(.width(2), .enable("false")) multiplexer_2 (
    .in0(2'b00), .in1(priority_encoder_1_out), .out(multiplexer_2_out), .sel(priority_encoder_1_gs));
  Multiplexer #(.enable("false")) multiplexer_3 (
    .in0(priority_encoder_1_gs), .in1(in_2), .out(multiplexer_3_out), .sel(comparator_2_gt));
  Multiplexer #(.enable("false")) multiplexer_4 (
    .in0(multiplexer_3_out), .in1(1'b1), .out(multiplexer_4_out), .sel(comparator_1_lt));
  // Probe on reset
  Register #(.width(2)) register_1 (
    .D(multiplexer_2_out), .en(multiplexer_4_out), .Q(reset), .clk(clock));  // open: clr
  Comparator #(.width(2), .mode("unsigned")) comparator_1 (
    .a(reset), .b(multiplexer_2_out), .lt(comparator_1_lt));  // open: gt, eq
  Comparator #(.width(2), .mode("unsigned")) comparator_2 (.a(reset), .b(2'b00), .gt(comparator_2_gt));  // open: eq, lt
endmodule

module IF_ID (
  input  [31:0] pc_in,
  input  [31:0] ir_in,
  input  clk,
  output [31:0] pc_out,
  output [31:0] ir_out
);

  Register #(.width(32)) register_1 (.D(pc_in), .Q(pc_out), .clk(clk));  // open: en, clr
  Register #(.width(32)) register_2 (.D(ir_in), .Q(ir_out), .clk(clk));  // open: en, clr
endmodule

module ID_EX (
  input  Shamt_in,
  input  [3:0] Aluop_in,
  input  AluSrc_in,
  input  [31:0] R1_in,
  input  beq_in,
  input  bne_in,
  input  [1:0] RegDst_in,
  input  RegWrite_in,
  input  [31:0] R2_in,
  input  MemWrite_in,
  input  MemRead_in,
  input  [1:0] toReg_in,
  input  lh_in,
  input  srav_in,
  input  BGEZ_in,
  input  [31:0] shamt_in_2,
  input  pause_in,
  input  mfc0_in,
  input  mtc0_in,
  input  [31:0] immediate_in,
  input  [31:0] PC_in,
  input  clk,
  output Shamt_out,
  output [3:0] Aluop_out,
  output AluSrc_out,
  output [31:0] R1_out,
  output beq_out,
  output bne_out,
  output [1:0] RegDst_out,
  output RegWrite_out,
  output MemWrite_out,
  output [31:0] R2_out,
  output MemRead_out,
  output [1:0] toReg_out,
  output lh_out,
  output srav_out,
  output BGEZ_out,
  output pause_out,
  output [31:0] shamt_out_2,
  output mfc0_out,
  output mtc0_out,
  output [31:0] immediate_out,
  output [31:0] PC_out
);

  wire [31:21] register_6_q, undriven;

  Register #(.width(32)) register_1 (.D(R1_in), .Q(R1_out), .clk(clk));  // open: en, clr
  Register #(.width(32)) register_2 (.D(R2_in), .Q(R2_out), .clk(clk));  // open: en, clr
  Register #(.width(32)) register_3 (.D(shamt_in_2), .Q(shamt_out_2), .clk(clk));  // open: en, clr
  Register #(.width(32)) register_4 (.D(immediate_in), .Q(immediate_out), .clk(clk));  // open: en, clr
  Register #(.width(32)) register_5 (.D(PC_in), .Q(PC_out), .clk(clk));  // open: en, clr
  Register #(.width(32)) register_6 (
    .D({undriven, mtc0_in, mfc0_in, pause_in, BGEZ_in, srav_in, lh_in, toReg_in, MemRead_in, MemWrite_in, RegWrite_in, RegDst_in, bne_in, beq_in, AluSrc_in, Aluop_in, Shamt_in}),
    .Q({register_6_q, mtc0_out, mfc0_out, pause_out, BGEZ_out, srav_out, lh_out, toReg_out, MemRead_out, MemWrite_out, RegWrite_out, RegDst_out, bne_out, beq_out, AluSrc_out, Aluop_out, Shamt_out}),
    .clk(clk));  // open: en, clr
endmodule

module EX_Mem (
  input  [31:0] PC_in,
  input  [31:0] AluResult_in,
  input  [1:0] RegDst_in,
  input  RegWrite_in,
  input  MemWrite_in,
  input  MemRead_in,
  input  [1:0] toReg_in,
  input  lh_in,
  input  mfc0_in,
  input  mtc0_in,
  input  [31:0] R1_in,
  input  clk,
  output [31:0] PC_out,
  output [31:0] AluResult_out,
  output [1:0] RegDst_out,
  output RegWrite_out,
  output MemWrite_out,
  output MemRead_out,
  output [1:0] toReg_out,
  output lh_out,
  output mfc0_out,
  output mfc0_out_2,
  output [31:0] R1_out
);

  wire [31:0] register_4_q, undriven;

  Register #(.width(32)) register_1 (.D(R1_in), .Q(R1_out), .clk(clk));  // open: en, clr
  Register #(.width(32)) register_2 (.D(PC_in), .Q(PC_out), .clk(clk));  // open: en, clr
  Register #(.width(32)) register_3 (.D(AluResult_in), .Q(AluResult_out), .clk(clk));  // open: en, clr
  Register #(.width(32)) register_4 (
    .D({undriven[31:21], mtc0_in, mfc0_in, undriven[18:16], lh_in, toReg_in, MemRead_in, MemWrite_in, RegWrite_in, RegDst_in, undriven[7:0]}),
    .Q({register_4_q[31:21], mfc0_out_2, mfc0_out, register_4_q[18:16], lh_out, toReg_out, MemRead_out, MemWrite_out, RegWrite_out, RegDst_out, register_4_q[7:0]}),
    .clk(clk));  // open: en, clr
endmodule

module Mem_WB (
  input  [31:0] PC_in,
  input  [31:0] AluResult_in,
  input  [31:0] MemData_in,
  input  [1:0] RegDst_in,
  input  RegWrite_in,
  input  [1:0] toReg_in,
  input  mfc0_in,
  input  mtc0_in,
  input  clk,
  output [31:0] PC_out,
  output [31:0] AluResult_out,
  output [31:0] MemData_out,
  output [1:0] RegDst_out,
  output RegWrite_out,
  output [1:0] toReg_out,
  output mfc0_out,
  output mtc0_out
);

  wire [31:0] register_4_q, undriven;

  Register #(.width(32)) register_1 (.D(PC_in), .Q(PC_out), .clk(clk));  // open: en, clr
  Register #(.width(32)) register_2 (.D(AluResult_in), .Q(AluResult_out), .clk(clk));  // open: en, clr
  Register #(.width(32)) register_3 (.D(MemData_in), .Q(MemData_out), .clk(clk));  // open: en, clr
  Register #(.width(32)) register_4 (
    .D({undriven[31:21], mtc0_in, mfc0_in, undriven[18:15], toReg_in, undriven[12:11], RegWrite_in, RegDst_in, undriven[7:0]}),
    .Q({register_4_q[31:21], mtc0_out, mfc0_out, register_4_q[18:15], toReg_out, register_4_q[12:11], RegWrite_out, RegDst_out, register_4_q[7:0]}),
    .clk(clk));  // open: en, clr
endmodule
