// Logisim project ACM1401_U201414620_胡汉鹏_alu.circ as structural Verilog: 8 circuits, main circuit ALU
module ALU (
  input  [31:0] X,
  input  [31:0] Y,
  input  [3:0] AluOP,
  output Signed_Overflow,
  output UnSigned_Overflow,
  output Equal,
  output [31:0] Result,
  output [31:0] Result_2
);

  wire and_2_out, and_3_out, and_4_out, and_5_out, and_6_out, and_7_out, bitselector_1_out,
       bitselector_2_out, bitselector_3_out, n32bit_adder_1_cn_star, or_3_out, or_4_out, X_Y;
  wire [0:0] comparator_1_lt;
  wire [31:0] and_1_out, B, divider_1_out, divider_1_rem, F, multiplier_1_cout, multiplier_1_out, nor_1_out,
       not_1_out, or_1_out, shifter_1_out, shifter_2_out, shifter_3_out, xor_1_out;

  // Probe on X
  // Probe on X
  // Probe on Y
  // Probe on Y
  // Probe on AluOP
  // Probe on Result
  // Probe on Result
  assign not_1_out = ~Y;  // NOT_Gate not_1, 32 bits wide
  _32bit_adder u_32bit_adder_1 (.F(F), .Cn_star(n32bit_adder_1_cn_star), .A(X), .B(B), .Cn(AluOP[1]));
  Multiplexer #(.select(2), .width(32)) multiplexer_1 (
    .in0({32{1'b0}}), .in1(Y), .in2(not_1_out), .in3({32{1'b0}}), .out(B), .sel(AluOP[1:0]), .en(1'b1));
  // Probe on AluOP[1:0]
  Comparator #(.width(32)) comparator_1 (.a(X), .b(Y), .lt(comparator_1_lt[0]));  // open: gt, eq
  Comparator #(.width(32), .mode("unsigned")) comparator_2 (.a(X), .b(Y), .eq(Equal), .lt(X_Y));  // open: gt
  // Probe on Result_2
  Shifter #(.width(32)) shifter_1 (.in(X), .\dist (Y[4:0]), .out(shifter_1_out));
  Shifter #(.width(32), .shift("ar")) shifter_2 (.in(X), .\dist (Y[4:0]), .out(shifter_2_out));
  Shifter #(.width(32), .shift("lr")) shifter_3 (.in(X), .\dist (Y[4:0]), .out(shifter_3_out));
  Multiplier #(.width(32)) multiplier_1 (.a(X), .b(Y), .out(multiplier_1_out), .cout(multiplier_1_cout));  // open: cin
  Divider #(.width(32)) divider_1 (.a(X), .b(Y), .out(divider_1_out), .rem(divider_1_rem));  // open: upper
  assign and_1_out = X & Y;  // AND_Gate and_1, 32 bits wide
  assign or_1_out = X | Y;  // OR_Gate or_1, 32 bits wide
  assign xor_1_out = X ^ Y;  // XOR_Gate xor_1, 32 bits wide
  assign nor_1_out = ~(X | Y);  // NOR_Gate nor_1, 32 bits wide
  Multiplexer #(.select(4), .width(32)) multiplexer_2 (
    .in0(shifter_1_out), .in1(shifter_2_out), .in2(shifter_3_out), .in3(multiplier_1_out),
    .in4(divider_1_out), .in5(F), .in6(F), .in7(and_1_out), .in8(or_1_out), .in9(xor_1_out),
    .in10(nor_1_out), .in11({{31{1'b0}}, comparator_1_lt[0]}), .in12({{31{1'b0}}, X_Y}), .in13({32{1'b0}}),
    .in14({32{1'b0}}), .in15({32{1'b0}}), .out(Result), .sel(AluOP), .en(1'b1));
  BitSelector #(.width(32)) bitselector_1 (.in(X), .out(bitselector_1_out), .sel({5{1'b1}}));
  BitSelector #(.width(32)) bitselector_2 (.in(B), .out(bitselector_2_out), .sel({5{1'b1}}));
  BitSelector #(.width(32)) bitselector_3 (.in(F), .out(bitselector_3_out), .sel({5{1'b1}}));
  Multiplexer #(.select(4), .width(32)) multiplexer_3 (
    .in0({32{1'b0}}), .in1({32{1'b0}}), .in2({32{1'b0}}), .in3(multiplier_1_cout), .in4(divider_1_rem),
    .in5({32{1'b0}}), .in6({32{1'b0}}), .in7({32{1'b0}}), .in8({32{1'b0}}), .in9({32{1'b0}}),
    .in10({32{1'b0}}), .in11({32{1'b0}}), .in12({32{1'b0}}), .in13({32{1'b0}}), .in14({32{1'b0}}),
    .in15({32{1'b0}}), .out(Result_2), .sel(AluOP), .en(1'b1));
  and and_2 (and_2_out, ~AluOP[3], AluOP[2], ~AluOP[1], AluOP[0]);  // AND_Gate
  and and_3 (and_3_out, ~AluOP[3], AluOP[2], AluOP[1], ~AluOP[0]);  // AND_Gate
  and and_4 (and_4_out, bitselector_1_out, bitselector_2_out, ~bitselector_3_out);  // AND_Gate
  and and_5 (and_5_out, ~bitselector_1_out, ~bitselector_2_out, bitselector_3_out);  // AND_Gate
  and and_6 (and_6_out, n32bit_adder_1_cn_star, and_2_out);
  or or_2 (UnSigned_Overflow, and_6_out, and_7_out);
  and and_7 (and_7_out, and_3_out, X_Y);
  or or_3 (or_3_out, and_2_out, and_3_out);
  and and_8 (Signed_Overflow, or_3_out, or_4_out);
  or or_4 (or_4_out, and_4_out, and_5_out);

  // Other names for the same wires on the sheet: A[31:0] = X; OF = Signed_Overflow; Result2[31:0] = Result_2;
  //   S[3:0] = AluOP; UOF = UnSigned_Overflow

  // Notes on the sheet:
  //   不要改变此引脚区域内容，也不要改变ALU封装形式
  //   输入引脚
  //   请在下方利用上方输入输出引脚的隧道信号构建ALU电路，ctrl+d复制选择部件
  //   华中科技大学计算机学院 计算机组成原理，鸣谢加州大学伯克利CS61C课程
  //   输出引脚
  //   探测区域
endmodule

module \演示电路  (
  input  [31:0] X,
  input  [31:0] Y,
  input  [3:0] ALUOP,
  output Signed_Overflow,
  output Unsigned_overflow,
  output [31:0] Result,
  output [31:0] Result_2,
  output Equal
);

  // Probe on X
  // Probe on X
  ALU alu_1 (
    .AluOP(ALUOP), .X(X), .Equal(Equal), .Result(Result), .Signed_Overflow(Signed_Overflow), .Y(Y),
    .Result_2(Result_2), .UnSigned_Overflow(Unsigned_overflow));
  // Probe on ALUOP
  // Probe on Y
  // Probe on Y
  // Probe on Result
  // Probe on Result
  // Probe on Result_2

  // Notes on the sheet:
  //   ALu电路无需调整位置即可连接在该电路中，并且不能出现蓝色线缆和三态输出
endmodule

module \等差数列  (
  input  [31:0] \数列初始值 ,
  input  [31:0] \等差值 ,
  input  \时钟 ,
  output [31:0] Result
);

  // Probe on \数列初始值 
  // Probe on \数列初始值 
  // Probe on \等差值 
  // Probe on \等差值 
  // Probe on Result
  // Probe on Result

  // Other names for the same wires on the sheet: 数列初值[31:0] = \数列初始值 ; 累加和[31:0] = Result

  // Notes on the sheet:
  //   不要改变此引脚区域内容，也不要改变ALU封装形式
  //   请在下方利用上方输入输出引脚的隧道信号构建等差数列求和电路，ctrl+d复制选择部件
  //   华中科技大学计算机学院 计算机组成原理，鸣谢加州大学伯克利CS61C课程
  //   输出引脚
  //   探测区域
endmodule

module SN74182 (
  input  P3,
  input  G3,
  input  P2,
  input  G2,
  input  P1,
  input  G1,
  input  P0,
  input  G0,
  input  Cn,
  output nP_star,
  output nG_star,
  output Cn_z,
  output Cn_y,
  output Cn_x
);

  wire and_1_out, and_2_out, and_3_out, and_4_out, and_5_out, and_6_out, and_7_out, and_8_out, and_9_out,
       and_10_out, and_11_out, and_12_out, and_13_out, not_1_out, not_2_out, not_3_out, not_4_out, not_5_out,
       not_6_out, not_7_out, not_8_out, not_9_out;

  or or_1 (nP_star, not_1_out, not_3_out, not_5_out, not_6_out);
  and and_1 (and_1_out, not_5_out, not_2_out, not_4_out, not_7_out);
  and and_2 (and_2_out, not_2_out, not_4_out, not_7_out, not_9_out);
  nor nor_1 (nG_star, and_2_out, and_1_out, and_3_out, and_5_out);
  and and_3 (and_3_out, not_3_out, not_2_out, not_4_out);
  not not_1 (not_1_out, P3);
  and and_4 (and_4_out, not_4_out, not_7_out, not_9_out, not_8_out);
  and and_5 (and_5_out, not_1_out, not_2_out);
  not not_2 (not_2_out, G3);
  nor nor_2 (Cn_z, and_4_out, and_6_out, and_8_out, and_7_out);
  and and_6 (and_6_out, not_6_out, not_4_out, not_7_out, not_9_out);
  and and_7 (and_7_out, not_3_out, not_4_out);
  and and_8 (and_8_out, not_5_out, not_7_out, not_4_out);
  not not_3 (not_3_out, P2);
  not not_4 (not_4_out, G2);
  nor nor_3 (Cn_y, and_10_out, and_9_out, and_12_out);
  and and_9 (and_9_out, not_6_out, not_7_out, not_9_out);
  and and_10 (and_10_out, not_7_out, not_9_out, not_8_out);
  not not_5 (not_5_out, P1);
  nor nor_4 (Cn_x, and_11_out, and_13_out);
  and and_11 (and_11_out, not_9_out, not_8_out);
  and and_12 (and_12_out, not_5_out, not_7_out);
  not not_6 (not_6_out, P0);
  not not_7 (not_7_out, G1);
  and and_13 (and_13_out, not_6_out, not_9_out);
  not not_8 (not_8_out, Cn);
  not not_9 (not_9_out, G0);
endmodule

module _4bit_adder (
  input  A0,
  input  A1,
  input  A2,
  input  A3,
  input  B0,
  input  B1,
  input  B2,
  input  B3,
  input  Cn,
  output F0,
  output F1,
  output F2,
  output F3,
  output P,
  output G,
  output Cn4
);

  wire and_1_out, and_2_out, and_3_out, and_4_out, and_5_out, and_6_out, and_7_out, and_9_out, and_10_out,
       and_11_out, and_12_out, and_13_out, and_14_out, and_15_out, and_16_out, and_17_out, and_18_out,
       and_19_out, and_20_out, and_21_out, and_22_out, and_23_out, and_24_out, or_1_out, or_2_out, or_3_out,
       or_4_out, or_5_out, or_6_out, or_7_out, or_8_out, or_9_out, or_10_out, or_11_out, or_12_out,
       or_13_out, or_14_out, or_15_out, or_16_out, or_17_out, or_18_out, or_19_out, or_20_out, or_21_out,
       or_22_out, or_23_out, or_24_out, or_25_out, or_26_out, or_27_out, or_28_out, or_29_out, or_30_out,
       or_31_out;

  xor odd_parity_1 (F0, A0, B0, Cn);
  or or_1 (or_1_out, A0, B0);
  or or_2 (or_2_out, A1, B1);
  or or_3 (or_3_out, A1, B1);
  or or_4 (or_4_out, A0, B0);
  or or_5 (or_5_out, A1, B1);
  or or_6 (or_6_out, A3, B3);
  or or_7 (or_7_out, A2, B2);
  or or_8 (or_8_out, A1, B1);
  or or_9 (or_9_out, A0, B0);
  or or_10 (or_10_out, A1, B1);
  or or_11 (or_11_out, A1, B1);
  and and_1 (and_1_out, A0, B0);
  and and_2 (and_2_out, or_1_out, Cn);
  and and_3 (and_3_out, A1, B1);
  and and_4 (and_4_out, or_2_out, A0, B0);
  and and_5 (and_5_out, or_3_out, or_4_out, Cn);
  and and_6 (and_6_out, A1, B1);
  and and_7 (and_7_out, or_5_out, A0, B0);
  and and_8 (P, or_6_out, or_7_out, or_8_out, or_9_out);
  and and_9 (and_9_out, A1, B1);
  and and_10 (and_10_out, or_10_out, A0, B0);
  and and_11 (and_11_out, A1, B1);
  and and_12 (and_12_out, or_11_out, A0, B0);
  or or_12 (or_12_out, and_1_out, and_2_out);
  or or_13 (or_13_out, and_3_out, and_4_out, and_5_out);
  or or_14 (or_14_out, A2, B2);
  or or_15 (or_15_out, and_6_out, and_7_out);
  or or_16 (or_16_out, A2, B2);
  or or_17 (or_17_out, A1, B1);
  or or_18 (or_18_out, A0, B0);
  or or_19 (or_19_out, A2, B2);
  or or_20 (or_20_out, and_9_out, and_10_out);
  or or_21 (or_21_out, A2, B2);
  or or_22 (or_22_out, and_11_out, and_12_out);
  xor odd_parity_2 (F1, A1, B1, or_12_out);
  xor odd_parity_3 (F2, A2, B2, or_13_out);
  and and_13 (and_13_out, A2, B2);
  and and_14 (and_14_out, or_14_out, or_15_out);
  or or_23 (or_23_out, and_13_out, and_14_out, and_15_out);
  and and_15 (and_15_out, or_16_out, or_17_out, or_18_out, Cn);
  or or_24 (or_24_out, A3, B3);
  and and_16 (and_16_out, A2, B2);
  or or_25 (or_25_out, and_16_out, and_17_out);
  and and_17 (and_17_out, or_19_out, or_20_out);
  or or_26 (or_26_out, A3, B3);
  and and_18 (and_18_out, A2, B2);
  or or_27 (or_27_out, and_18_out, and_19_out);
  and and_19 (and_19_out, or_21_out, or_22_out);
  or or_28 (or_28_out, B3, A3);
  or or_29 (or_29_out, A2, B2);
  or or_30 (or_30_out, A1, B1);
  or or_31 (or_31_out, A0, B0);
  xor odd_parity_4 (F3, A3, B3, or_23_out);
  and and_20 (and_20_out, A3, B3);
  and and_21 (and_21_out, or_24_out, or_25_out);
  and and_22 (and_22_out, A3, B3);
  and and_23 (and_23_out, or_26_out, or_27_out);
  and and_24 (and_24_out, or_28_out, or_29_out, or_30_out, or_31_out, Cn);
  or or_32 (G, and_20_out, and_21_out);
  or or_33 (Cn4, and_22_out, and_23_out, and_24_out);
endmodule

module _16bit_adder (
  input  Cn,
  input  [15:0] A,
  input  [15:0] B,
  output G_star,
  output P_star,
  output [15:0] F,
  output Cn_4
);

  wire Cx, Cy, Cz, n4bit_adder_1_g, n4bit_adder_1_p, n4bit_adder_2_g, n4bit_adder_2_p, n4bit_adder_3_g,
       n4bit_adder_3_p, n4bit_adder_4_g, n4bit_adder_4_p, sn74182_1_np_star;

  not not_1 (P_star, sn74182_1_np_star);
  // Probe on F
  // Probe on A
  // Probe on B
  SN74182 sn74182_1 (
    .nP_star(sn74182_1_np_star), .nG_star(G_star), .Cn_z(Cz), .Cn_y(Cy), .Cn_x(Cx), .P3(n4bit_adder_1_p),
    .G3(n4bit_adder_1_g), .P2(n4bit_adder_2_p), .G2(n4bit_adder_2_g), .P1(n4bit_adder_3_p),
    .G1(n4bit_adder_3_g), .P0(n4bit_adder_4_p), .G0(n4bit_adder_4_g), .Cn(Cn));
  _4bit_adder u_4bit_adder_1 (
    .A0(A[12]), .A1(A[13]), .A2(A[14]), .A3(A[15]), .B0(B[12]), .B1(B[13]), .B2(B[14]), .B3(B[15]), .Cn(Cz),
    .F0(F[12]), .F1(F[13]), .F2(F[14]), .F3(F[15]), .P(n4bit_adder_1_p), .G(n4bit_adder_1_g), .Cn4(Cn_4));
  _4bit_adder u_4bit_adder_2 (
    .A0(A[8]), .A1(A[9]), .A2(A[10]), .A3(A[11]), .B0(B[8]), .B1(B[9]), .B2(B[10]), .B3(B[11]), .Cn(Cy),
    .F0(F[8]), .F1(F[9]), .F2(F[10]), .F3(F[11]), .P(n4bit_adder_2_p), .G(n4bit_adder_2_g));  // open: Cn4
  _4bit_adder u_4bit_adder_3 (
    .A0(A[4]), .A1(A[5]), .A2(A[6]), .A3(A[7]), .B0(B[4]), .B1(B[5]), .B2(B[6]), .B3(B[7]), .Cn(Cx),
    .F0(F[4]), .F1(F[5]), .F2(F[6]), .F3(F[7]), .P(n4bit_adder_3_p), .G(n4bit_adder_3_g));  // open: Cn4
  _4bit_adder u_4bit_adder_4 (
    .A0(A[0]), .A1(A[1]), .A2(A[2]), .A3(A[3]), .B0(B[0]), .B1(B[1]), .B2(B[2]), .B3(B[3]), .Cn(Cn),
    .F0(F[0]), .F1(F[1]), .F2(F[2]), .F3(F[3]), .P(n4bit_adder_4_p), .G(n4bit_adder_4_g));  // open: Cn4
endmodule

module _32bit_adder (
  input  Cn,
  input  [31:0] A,
  input  [31:0] B,
  output [31:0] F,
  output Cn_star
);

  wire and_1_out, n16bit_adder_2_g_star, n16bit_adder_2_p_star, or_1_out;

  // Probe on F
  // Probe on A
  // Probe on B
  // Probe on F[31:16]
  _16bit_adder u_16bit_adder_1 (
    .F(F[31:16]), .Cn_4(Cn_star), .A(B[31:16]), .B(A[31:16]), .Cn(or_1_out));  // open: G_star, P_star
  and and_1 (and_1_out, Cn, n16bit_adder_2_p_star);
  or or_1 (or_1_out, and_1_out, n16bit_adder_2_g_star);
  _16bit_adder u_16bit_adder_2 (
    .G_star(n16bit_adder_2_g_star), .P_star(n16bit_adder_2_p_star), .F(F[15:0]), .A(B[15:0]), .B(A[15:0]),
    .Cn(Cn));  // open: Cn_4
endmodule

module myalu (
  input  [31:0] in_1,
  input  [31:0] in_2,
  output [31:0] out
);

  wire clock_1_out, register_1_q;
  wire [31:0] multiplexer_1_out, register_2_q, register_3_q, Rout;

  Register #(.width(1)) register_1 (.D(1'b1), .Q(register_1_q), .clk(clock_1_out));  // open: en, clr
  // Probe on in_2
  // Probe on in_1
  Register #(.width(32)) register_2 (.D(Rout), .Q(register_2_q), .clk(clock_1_out));  // open: en, clr
  Clock clock_1 (.out(clock_1_out));
  // Probe on Rout
  Multiplexer #(.width(32)) multiplexer_1 (
    .in0(in_2), .in1(register_2_q), .out(multiplexer_1_out), .sel(register_1_q), .en(1'b1));
  // Probe on Rout
  ALU alu_1 (
    .AluOP(4'b0101), .X(in_1), .Result(Rout), .Y(multiplexer_1_out));  // open: Equal, Signed_Overflow, Result_2, UnSigned_Overflow
  Register #(.width(32)) register_3 (.D(out), .Q(register_3_q), .clk(clock_1_out));  // open: en, clr
  ALU alu_2 (
    .AluOP(4'b0101), .X(multiplexer_1_out), .Result(out), .Y(register_3_q));  // open: Equal, Signed_Overflow, Result_2, UnSigned_Overflow
  // Probe on out

  // Other names for the same wires on the sheet: Result[31:0] = out
endmodule
